// Logisim project DigitosPares0a10 Versao Video.circ as structural Verilog: 4 circuits, main circuit main
module main (
  input  in_1,
  input  in_2,
  output [2:0] out_3
);

  wire button_1_out, clock_1_out, digitosdezena_1_a, digitosdezena_1_b, digitosdezena_1_c, digitosdezena_1_d,
       digitosdezena_1_e, digitosdezena_1_f, seleciona1_ou_0_1_saidaunica, unitdigits_1_a, unitdigits_1_b,
       unitdigits_1_c, unitdigits_1_d, unitdigits_1_e, unitdigits_1_f, unitdigits_1_g;

  Counter #(.width(3), .max('h5), .trigger("falling")) counter_1 (
    .load(in_1), .count(in_2), .Q(out_3), .clk(clock_1_out), .clr(button_1_out));  // open: D, carry
  Clock clock_1 (.out(clock_1_out));
  Button button_1 (.out(button_1_out));
  Seleciona1_ou_0 seleciona1_ou_0_1 (.Bit2(out_3[2]), .Bit0(out_3[0]), .SaidaUnica(seleciona1_ou_0_1_saidaunica));
  DigitosDezena digitosdezena_1 (
    .bit0(seleciona1_ou_0_1_saidaunica), .a(digitosdezena_1_a), .b(digitosdezena_1_b), .c(digitosdezena_1_c),
    .d(digitosdezena_1_d), .e(digitosdezena_1_e), .f(digitosdezena_1_f));
  _7_Segment_Display u_7_segment_display_1 (
    .f(digitosdezena_1_f), .a(digitosdezena_1_a), .b(digitosdezena_1_b), .e(digitosdezena_1_e),
    .d(digitosdezena_1_d), .c(digitosdezena_1_c));  // open: g, dp
  _7_Segment_Display u_7_segment_display_2 (
    .g(unitdigits_1_g), .f(unitdigits_1_f), .a(unitdigits_1_a), .b(unitdigits_1_b), .e(unitdigits_1_e),
    .d(unitdigits_1_d), .c(unitdigits_1_c));  // open: dp
  UnitDigits unitdigits_1 (
    .Bit2(out_3[2]), .Bit1(out_3[1]), .Bit0(out_3[0]), .a(unitdigits_1_a), .b(unitdigits_1_b),
    .c(unitdigits_1_c), .d(unitdigits_1_d), .e(unitdigits_1_e), .f(unitdigits_1_f), .g(unitdigits_1_g));
endmodule

module UnitDigits (
  input  Bit2,
  input  Bit1,
  input  Bit0,
  output a,
  output b,
  output c,
  output d,
  output e,
  output f,
  output g
);

  wire and_1_out, and_2_out, and_3_out, and_4_out, and_5_out, and_6_out, and_7_out, and_8_out, and_9_out,
       and_10_out, and_11_out, and_12_out, and_13_out, not_1_out, not_2_out, not_3_out, not_4_out, not_5_out,
       not_6_out, not_7_out, not_8_out, not_9_out, not_10_out, not_11_out, not_12_out, not_13_out,
       not_14_out, not_15_out, not_16_out, not_17_out, not_18_out, not_19_out, not_20_out, not_21_out;

  not not_1 (not_1_out, Bit2);
  not not_2 (not_2_out, Bit2);
  not not_3 (not_3_out, Bit0);
  not not_4 (not_4_out, Bit2);
  not not_5 (not_5_out, Bit0);
  not not_6 (not_6_out, Bit2);
  not not_7 (not_7_out, Bit1);
  not not_8 (not_8_out, Bit2);
  not not_9 (not_9_out, Bit2);
  not not_10 (not_10_out, Bit2);
  not not_11 (not_11_out, Bit0);
  not not_12 (not_12_out, Bit2);
  not not_13 (not_13_out, Bit1);
  not not_14 (not_14_out, Bit2);
  not not_15 (not_15_out, Bit2);
  not not_16 (not_16_out, Bit1);
  not not_17 (not_17_out, Bit0);
  not not_18 (not_18_out, Bit1);
  and and_1 (and_1_out, not_1_out, Bit0);
  and and_2 (and_2_out, not_2_out, not_3_out);
  not not_19 (not_19_out, Bit1);
  and and_3 (and_3_out, not_4_out, not_5_out);
  and and_4 (and_4_out, not_6_out, Bit1);
  and and_5 (and_5_out, Bit2, not_7_out);
  not not_20 (not_20_out, Bit1);
  and and_6 (and_6_out, not_8_out, Bit0);
  not not_21 (not_21_out, Bit1);
  and and_7 (and_7_out, not_9_out, Bit0);
  and and_8 (and_8_out, not_10_out, not_11_out);
  and and_9 (and_9_out, not_12_out, Bit1);
  and and_10 (and_10_out, Bit2, not_13_out);
  and and_11 (and_11_out, not_14_out, Bit0);
  and and_12 (and_12_out, not_15_out, Bit1);
  and and_13 (and_13_out, Bit2, not_16_out, not_17_out);
  or or_1 (a, not_18_out, and_1_out);
  or or_2 (b, and_2_out, not_19_out);
  or or_3 (c, and_3_out, and_4_out, and_5_out);
  or or_4 (d, not_20_out, and_6_out);
  or or_5 (e, not_21_out, and_7_out);
  or or_6 (f, and_8_out, and_9_out, and_10_out);
  or or_7 (g, and_11_out, and_12_out, and_13_out);
endmodule

module DigitosDezena (
  input  bit0,
  output a,
  output b,
  output c,
  output d,
  output e,
  output f
);

  not not_1 (a, bit0);
  not not_2 (d, bit0);
  not not_3 (e, bit0);
  not not_4 (f, bit0);

  assign b = 1'b1;
  assign c = 1'b1;
endmodule

module Seleciona1_ou_0 (
  input  Bit2,
  input  Bit0,
  output SaidaUnica
);

  and and_1 (SaidaUnica, Bit2, Bit0);
endmodule
