// Logisim project DigitosPares0a10.circ as structural Verilog: 3 circuits, main circuit DigitosUnidades
module main (
  input  Reverte,
  input  Pausa__no_zero,
  output out_3,
  output out_4,
  output out_5,
  output out_6
);

  wire and_1_out, clock_1_out, digitosdezenas_1_a, digitosdezenas_1_b, digitosdezenas_1_c,
       digitosdezenas_1_d, digitosdezenas_1_e, digitosdezenas_1_f, digitosdezenas_1_g, digitosunidades_1_a,
       digitosunidades_1_b, digitosunidades_1_c, digitosunidades_1_d, digitosunidades_1_e,
       digitosunidades_1_f, digitosunidades_1_g, Reinicia_out;

  Clock #(.highDuration(5)) clock_1 (.out(clock_1_out));
  Button Reinicia (.out(Reinicia_out));
  Counter #(.width(4), .max('hb)) counter_1 (
    .load(Reverte), .count(Pausa__no_zero), .Q({out_3, out_4, out_5, out_6}), .clk(clock_1_out),
    .clr(Reinicia_out));  // open: D, carry
  and and_1 (and_1_out, out_5, out_3);
  DigitosDezenas digitosdezenas_1 (
    .BitParidade(out_6), .Bit0(and_1_out), .a(digitosdezenas_1_a), .b(digitosdezenas_1_b),
    .c(digitosdezenas_1_c), .d(digitosdezenas_1_d), .e(digitosdezenas_1_e), .f(digitosdezenas_1_f),
    .g(digitosdezenas_1_g));
  _7_Segment_Display u_7_segment_display_1 (
    .g(digitosdezenas_1_g), .f(digitosdezenas_1_f), .a(digitosdezenas_1_a), .b(digitosdezenas_1_b),
    .e(digitosdezenas_1_e), .d(digitosdezenas_1_d), .c(digitosdezenas_1_c));  // open: dp
  _7_Segment_Display u_7_segment_display_2 (
    .g(digitosunidades_1_g), .f(digitosunidades_1_f), .a(digitosunidades_1_a), .b(digitosunidades_1_b),
    .e(digitosunidades_1_e), .d(digitosunidades_1_d), .c(digitosunidades_1_c));  // open: dp
  DigitosUnidades digitosunidades_1 (
    .Bit3(out_3), .Bit2(out_4), .Bit1(out_5), .Bit0(out_6), .a(digitosunidades_1_a), .b(digitosunidades_1_b),
    .c(digitosunidades_1_c), .d(digitosunidades_1_d), .e(digitosunidades_1_e), .f(digitosunidades_1_f),
    .g(digitosunidades_1_g));
endmodule

module DigitosUnidades (
  input  Bit3,
  input  Bit2,
  input  Bit1,
  input  Bit0,
  output a,
  output b,
  output c,
  output d,
  output e,
  output f,
  output g
);

  wire and_1_out, and_2_out, and_3_out, and_4_out, and_5_out, and_6_out, and_7_out, and_8_out, and_9_out,
       and_10_out, and_11_out, and_12_out, and_13_out, and_14_out, and_15_out, and_16_out, and_17_out,
       not_1_out, not_2_out, not_3_out, not_4_out, not_5_out, not_6_out, not_7_out, not_8_out, not_9_out,
       not_10_out, not_11_out, not_12_out, not_13_out, not_14_out, not_15_out, not_16_out, not_17_out,
       not_18_out, not_19_out, not_20_out, not_21_out, not_22_out, not_23_out, not_24_out, not_25_out,
       not_26_out, not_27_out, not_28_out, not_29_out, not_30_out, not_31_out, not_32_out, not_33_out,
       not_34_out, not_35_out, not_36_out, not_37_out, not_38_out;

  not not_1 (not_1_out, Bit2);
  and and_1 (and_1_out, not_1_out, not_2_out);
  not not_2 (not_2_out, Bit0);
  not not_3 (not_3_out, Bit3);
  and and_2 (and_2_out, not_3_out, Bit1, not_4_out);
  not not_4 (not_4_out, Bit0);
  not not_5 (not_5_out, Bit3);
  not not_6 (not_6_out, Bit1);
  and and_3 (and_3_out, not_5_out, not_6_out, not_7_out);
  not not_7 (not_7_out, Bit0);
  not not_8 (not_8_out, Bit2);
  and and_4 (and_4_out, not_8_out, not_9_out);
  not not_9 (not_9_out, Bit0);
  not not_10 (not_10_out, Bit3);
  and and_5 (and_5_out, not_10_out, not_11_out, not_12_out);
  not not_11 (not_11_out, Bit1);
  not not_12 (not_12_out, Bit0);
  not not_13 (not_13_out, Bit3);
  and and_6 (and_6_out, not_13_out, Bit2, not_14_out);
  not not_14 (not_14_out, Bit0);
  not not_15 (not_15_out, Bit2);
  and and_7 (and_7_out, Bit3, not_15_out, not_16_out);
  not not_16 (not_16_out, Bit0);
  not not_17 (not_17_out, Bit2);
  and and_8 (and_8_out, not_17_out, not_18_out);
  not not_18 (not_18_out, Bit0);
  not not_19 (not_19_out, Bit3);
  and and_9 (and_9_out, not_19_out, Bit1, not_20_out);
  not not_20 (not_20_out, Bit0);
  not not_21 (not_21_out, Bit2);
  and and_10 (and_10_out, not_21_out, not_22_out);
  not not_22 (not_22_out, Bit0);
  not not_23 (not_23_out, Bit3);
  and and_11 (and_11_out, not_23_out, Bit1, not_24_out);
  not not_24 (not_24_out, Bit0);
  not not_25 (not_25_out, Bit3);
  not not_26 (not_26_out, Bit1);
  and and_12 (and_12_out, not_25_out, not_26_out, not_27_out);
  not not_27 (not_27_out, Bit0);
  not not_28 (not_28_out, Bit3);
  and and_13 (and_13_out, not_28_out, Bit2, not_29_out);
  not not_29 (not_29_out, Bit0);
  and and_14 (and_14_out, Bit3, not_30_out, not_31_out);
  not not_30 (not_30_out, Bit2);
  not not_31 (not_31_out, Bit0);
  not not_32 (not_32_out, Bit3);
  not not_33 (not_33_out, Bit0);
  not not_34 (not_34_out, Bit3);
  not not_35 (not_35_out, Bit0);
  not not_36 (not_36_out, Bit2);
  not not_37 (not_37_out, Bit1);
  not not_38 (not_38_out, Bit0);
  or or_1 (a, and_1_out, and_2_out);
  or or_2 (b, and_3_out, and_4_out);
  or or_3 (c, and_5_out, and_6_out, and_7_out);
  or or_4 (d, and_8_out, and_9_out);
  or or_5 (e, and_10_out, and_11_out);
  or or_6 (f, and_12_out, and_13_out, and_14_out);
  and and_15 (and_15_out, not_32_out, Bit1, not_33_out);
  or or_7 (g, and_15_out, and_16_out, and_17_out);
  and and_16 (and_16_out, not_34_out, Bit2, not_35_out);
  and and_17 (and_17_out, Bit3, not_36_out, not_37_out, not_38_out);
endmodule

module DigitosDezenas (
  input  BitParidade,
  input  Bit0,
  output a,
  output b,
  output c,
  output d,
  output e,
  output f,
  output g
);

  wire not_1_out, not_2_out, not_5_out, not_6_out, not_7_out, not_8_out, not_9_out, not_10_out;

  not not_1 (not_1_out, BitParidade);
  not not_2 (not_2_out, Bit0);
  not not_3 (b, BitParidade);
  not not_4 (c, BitParidade);
  not not_5 (not_5_out, BitParidade);
  not not_6 (not_6_out, Bit0);
  not not_7 (not_7_out, BitParidade);
  not not_8 (not_8_out, Bit0);
  not not_9 (not_9_out, BitParidade);
  not not_10 (not_10_out, Bit0);
  and and_1 (a, not_1_out, not_2_out);
  and and_2 (d, not_5_out, not_6_out);
  and and_3 (e, not_7_out, not_8_out);
  and and_4 (f, not_9_out, not_10_out);

  assign g = 1'b0;
endmodule
