// Logisim project Display de sete segmentos V2 31052020.circ as structural Verilog: 1 circuit, main circuit DisplaySeteSegmtos
module DisplaySeteSegmtos (
  input  in_1,
  input  in_2,
  input  in_3,
  input  in_4,
  output a,
  output b,
  output c,
  output d,
  output e,
  output f,
  output g
);

  wire and_1_out, and_2_out, and_3_out, and_4_out, and_5_out, and_6_out, button_1_out, button_2_out,
       clock_1_out, clock_2_out, clock_3_out, not_1_out, not_2_out, not_3_out, not_4_out, not_5_out,
       not_6_out, not_7_out, not_8_out, not_9_out, not_10_out, not_11_out, not_12_out, not_13_out,
       not_14_out, not_15_out, not_16_out, not_17_out, not_18_out, not_19_out, not_20_out, not_21_out,
       not_22_out, not_23_out, or_1_out, or_2_out, or_3_out, or_4_out, or_5_out, or_6_out, or_7_out,
       or_9_out, or_10_out, or_11_out, or_12_out, or_13_out, or_14_out, or_15_out, or_16_out;
  wire [3:0] Contador_q;

  Button button_1 (.out(button_1_out));
  Clock clock_1 (.out(clock_1_out));
  Button button_2 (.out(button_2_out));
  Clock #(.highDuration(20), .lowDuration(20)) clock_2 (.out(clock_2_out));
  and and_1 (and_1_out, clock_1_out, in_3);
  Clock #(.highDuration(60)) clock_3 (.out(clock_3_out));
  or or_1 (or_1_out, in_1, and_2_out);
  and and_2 (and_2_out, clock_2_out, in_2);
  or or_2 (or_2_out, button_1_out, and_1_out);
  or or_3 (or_3_out, button_2_out, and_3_out);
  and and_3 (and_3_out, clock_3_out, in_4);
  Counter #(.width(4), .max('ha), .trigger("falling")) Contador (
    .load(or_1_out), .Q(Contador_q), .clk(or_2_out), .clr(or_3_out));  // open: D, count, carry
  not not_1 (not_1_out, Contador_q[0]);
  not not_2 (not_2_out, Contador_q[2]);
  not not_3 (not_3_out, Contador_q[2]);
  not not_4 (not_4_out, Contador_q[0]);
  not not_5 (not_5_out, Contador_q[2]);
  not not_6 (not_6_out, Contador_q[1]);
  not not_7 (not_7_out, Contador_q[1]);
  not not_8 (not_8_out, Contador_q[0]);
  not not_9 (not_9_out, Contador_q[2]);
  not not_10 (not_10_out, Contador_q[2]);
  not not_11 (not_11_out, Contador_q[1]);
  not not_12 (not_12_out, Contador_q[0]);
  not not_13 (not_13_out, Contador_q[2]);
  not not_14 (not_14_out, Contador_q[3]);
  not not_15 (not_15_out, Contador_q[1]);
  not not_16 (not_16_out, Contador_q[0]);
  not not_17 (not_17_out, Contador_q[1]);
  not not_18 (not_18_out, Contador_q[1]);
  not not_19 (not_19_out, Contador_q[0]);
  not not_20 (not_20_out, Contador_q[2]);
  not not_21 (not_21_out, Contador_q[1]);
  not not_22 (not_22_out, Contador_q[0]);
  or or_4 (or_4_out, Contador_q[3], Contador_q[2], Contador_q[1], not_1_out);
  or or_5 (or_5_out, not_2_out, Contador_q[1], Contador_q[0]);
  or or_6 (or_6_out, not_3_out, Contador_q[1], not_4_out);
  or or_7 (or_7_out, not_5_out, not_6_out, Contador_q[0]);
  or or_8 (c, Contador_q[3], Contador_q[2], not_7_out, Contador_q[0]);
  or or_9 (or_9_out, Contador_q[3], Contador_q[2], Contador_q[1], not_8_out);
  or or_10 (or_10_out, not_9_out, Contador_q[1], Contador_q[0]);
  or or_11 (or_11_out, not_10_out, not_11_out, not_12_out);
  not not_23 (not_23_out, Contador_q[0]);
  or or_12 (or_12_out, not_13_out, Contador_q[1]);
  or or_13 (or_13_out, not_14_out, not_15_out);
  or or_14 (or_14_out, Contador_q[3], Contador_q[2], not_16_out);
  or or_15 (or_15_out, Contador_q[3], Contador_q[2], not_17_out);
  or or_16 (or_16_out, not_18_out, not_19_out);
  and and_4 (and_4_out, not_20_out, Contador_q[1]);
  and and_5 (and_5_out, Contador_q[2], not_21_out);
  and and_6 (and_6_out, Contador_q[2], not_22_out);
  and and_7 (a, or_4_out, or_5_out);
  and and_8 (b, or_6_out, or_7_out);
  and and_9 (d, or_9_out, or_10_out, or_11_out);
  and and_10 (e, not_23_out, or_12_out, or_13_out);
  and and_11 (f, or_14_out, or_15_out, or_16_out);
  or or_17 (g, and_4_out, and_5_out, and_6_out, Contador_q[3]);
  _7_Segment_Display u_7_segment_display_1 (.g(g), .f(f), .a(a), .b(b), .e(e), .d(d), .c(c));  // open: dp
endmodule
