// Logisim project Digitos0a15.circ as structural Verilog: 4 circuits, main circuit DigitosUnidades
module main (
  input  \Habilita_memória ,
  input  Reverte_contagem,
  input  Pausa,
  output out_4,
  output out_5,
  output out_6,
  output out_7
);

  wire Armazena_o_valor_corrente_out, Clock_out, digitosdezenas_1_a, digitosdezenas_1_b, digitosdezenas_1_c,
       digitosdezenas_1_d, digitosdezenas_1_e, digitosdezenas_1_f, digitosunidades_1_a, digitosunidades_1_b,
       digitosunidades_1_c, digitosunidades_1_d, digitosunidades_1_e, digitosunidades_1_f,
       digitosunidades_1_g, Reinicializa_contagem_out, selecionadigitodezena_1_a, \Zera_memória_out ;
  wire [3:0] \Memória_de_Valor_inicial__ou_final_se_reverso_q ;

  Button Armazena_o_valor_corrente (.out(Armazena_o_valor_corrente_out));
  Button \Zera_memória  (.out(\Zera_memória_out ));
  Clock #(.highDuration(5)) Clock (.out(Clock_out));
  Button Reinicializa_contagem (.out(Reinicializa_contagem_out));
  Counter #(.width(4), .max('hf), .ongoal("load")) counter_1 (
    .load(Reverte_contagem), .D(\Memória_de_Valor_inicial__ou_final_se_reverso_q ), .count(Pausa),
    .Q({out_4, out_5, out_6, out_7}), .clk(Clock_out), .clr(Reinicializa_contagem_out));  // open: carry
  Register #(.width(4)) \Memória_de_Valor_inicial__ou_final_se_reverso  (
    .D({out_4, out_5, out_6, out_7}), .en(\Habilita_memória ),
    .Q(\Memória_de_Valor_inicial__ou_final_se_reverso_q ), .clk(Armazena_o_valor_corrente_out),
    .clr(\Zera_memória_out ));
  SelecionaDigitoDezena selecionadigitodezena_1 (
    .Bit2(out_4), .Bit1(out_5), .Bit0(out_6), .a(selecionadigitodezena_1_a));
  DigitosDezenas digitosdezenas_1 (
    .Bit0(selecionadigitodezena_1_a), .a(digitosdezenas_1_a), .b(digitosdezenas_1_b), .c(digitosdezenas_1_c),
    .d(digitosdezenas_1_d), .e(digitosdezenas_1_e), .f(digitosdezenas_1_f));
  _7_Segment_Display u_7_segment_display_1 (
    .f(digitosdezenas_1_f), .a(digitosdezenas_1_a), .b(digitosdezenas_1_b), .e(digitosdezenas_1_e),
    .d(digitosdezenas_1_d), .c(digitosdezenas_1_c));  // open: g, dp
  _7_Segment_Display u_7_segment_display_2 (
    .g(digitosunidades_1_g), .f(digitosunidades_1_f), .a(digitosunidades_1_a), .b(digitosunidades_1_b),
    .e(digitosunidades_1_e), .d(digitosunidades_1_d), .c(digitosunidades_1_c));  // open: dp
  DigitosUnidades digitosunidades_1 (
    .Bit3(out_4), .Bit2(out_5), .Bit1(out_6), .Bit0(out_7), .a(digitosunidades_1_a), .b(digitosunidades_1_b),
    .c(digitosunidades_1_c), .d(digitosunidades_1_d), .e(digitosunidades_1_e), .f(digitosunidades_1_f),
    .g(digitosunidades_1_g));
endmodule

module DigitosUnidades (
  input  Bit3,
  input  Bit2,
  input  Bit1,
  input  Bit0,
  output a,
  output b,
  output c,
  output d,
  output e,
  output f,
  output g
);

  wire and_1_out, and_2_out, and_3_out, and_4_out, and_5_out, and_6_out, and_7_out, and_8_out, and_9_out,
       and_10_out, and_11_out, and_12_out, and_13_out, and_14_out, and_15_out, and_16_out, and_17_out,
       and_18_out, and_19_out, and_20_out, and_21_out, and_22_out, and_23_out, and_24_out, and_25_out,
       and_26_out, and_27_out, and_28_out, and_29_out, and_30_out, and_31_out, not_1_out, not_2_out,
       not_3_out, not_4_out, not_5_out, not_6_out, not_7_out, not_8_out, not_9_out, not_10_out, not_11_out,
       not_12_out, not_13_out, not_14_out, not_15_out, not_16_out, not_17_out, not_18_out, not_19_out,
       not_20_out, not_21_out, not_22_out, not_23_out, not_24_out, not_25_out, not_26_out, not_27_out,
       not_28_out, not_29_out, not_30_out, not_31_out, not_32_out, not_33_out, not_34_out, not_35_out,
       not_36_out, not_37_out, not_38_out, not_39_out, not_40_out, not_41_out, not_42_out, not_43_out,
       not_44_out;

  not not_1 (not_1_out, Bit2);
  and and_1 (and_1_out, not_1_out, not_2_out);
  not not_2 (not_2_out, Bit0);
  not not_3 (not_3_out, Bit3);
  and and_2 (and_2_out, not_3_out, Bit1);
  and and_3 (and_3_out, Bit2, Bit0);
  and and_4 (and_4_out, Bit3, not_4_out);
  not not_4 (not_4_out, Bit1);
  not not_5 (not_5_out, Bit2);
  not not_6 (not_6_out, Bit1);
  and and_5 (and_5_out, not_6_out, not_7_out);
  not not_7 (not_7_out, Bit0);
  not not_8 (not_8_out, Bit3);
  and and_6 (and_6_out, not_8_out, Bit1, Bit0);
  and and_7 (and_7_out, Bit3, not_9_out);
  not not_9 (not_9_out, Bit1);
  and and_8 (and_8_out, Bit3, not_10_out);
  not not_10 (not_10_out, Bit0);
  not not_11 (not_11_out, Bit3);
  and and_9 (and_9_out, not_11_out, not_12_out);
  not not_12 (not_12_out, Bit1);
  and and_10 (and_10_out, Bit2, Bit1);
  and and_11 (and_11_out, Bit3, not_13_out);
  not not_13 (not_13_out, Bit2);
  not not_14 (not_14_out, Bit2);
  and and_12 (and_12_out, not_14_out, not_15_out);
  not not_15 (not_15_out, Bit0);
  not not_16 (not_16_out, Bit3);
  and and_13 (and_13_out, not_16_out, not_17_out, Bit1);
  not not_17 (not_17_out, Bit2);
  not not_18 (not_18_out, Bit3);
  and and_14 (and_14_out, not_18_out, Bit1, not_19_out);
  not not_19 (not_19_out, Bit0);
  not not_20 (not_20_out, Bit1);
  and and_15 (and_15_out, Bit2, not_20_out, Bit0);
  not not_21 (not_21_out, Bit1);
  and and_16 (and_16_out, Bit3, not_21_out, not_22_out);
  not not_22 (not_22_out, Bit0);
  and and_17 (and_17_out, Bit3, Bit2, Bit0);
  not not_23 (not_23_out, Bit2);
  and and_18 (and_18_out, not_23_out, not_24_out);
  not not_24 (not_24_out, Bit0);
  not not_25 (not_25_out, Bit3);
  and and_19 (and_19_out, not_25_out, Bit1, not_26_out);
  not not_26 (not_26_out, Bit0);
  not not_27 (not_27_out, Bit1);
  and and_20 (and_20_out, Bit3, not_27_out, not_28_out);
  not not_28 (not_28_out, Bit0);
  not not_29 (not_29_out, Bit3);
  not not_30 (not_30_out, Bit1);
  and and_21 (and_21_out, not_29_out, not_30_out, not_31_out);
  not not_31 (not_31_out, Bit0);
  not not_32 (not_32_out, Bit3);
  and and_22 (and_22_out, not_32_out, Bit2, not_33_out);
  not not_33 (not_33_out, Bit1);
  not not_34 (not_34_out, Bit3);
  and and_23 (and_23_out, not_34_out, Bit2, not_35_out);
  not not_35 (not_35_out, Bit0);
  and and_24 (and_24_out, Bit3, not_36_out, not_37_out);
  not not_36 (not_36_out, Bit2);
  not not_37 (not_37_out, Bit1);
  and and_25 (and_25_out, Bit3, not_38_out, not_39_out);
  not not_38 (not_38_out, Bit2);
  not not_39 (not_39_out, Bit0);
  and and_26 (and_26_out, Bit3, Bit2, Bit1);
  not not_40 (not_40_out, Bit3);
  not not_41 (not_41_out, Bit2);
  and and_27 (and_27_out, not_40_out, not_41_out, Bit1);
  and and_28 (and_28_out, Bit2, not_42_out);
  not not_42 (not_42_out, Bit1);
  and and_29 (and_29_out, Bit2, not_43_out);
  not not_43 (not_43_out, Bit0);
  and and_30 (and_30_out, Bit3, not_44_out);
  not not_44 (not_44_out, Bit1);
  and and_31 (and_31_out, Bit3, Bit2);
  or or_1 (a, and_1_out, and_2_out, and_3_out, and_4_out);
  or or_2 (b, not_5_out, and_5_out, and_6_out, and_7_out, and_8_out);
  or or_3 (c, and_9_out, Bit0, and_10_out, and_11_out);
  or or_4 (e, and_18_out, and_19_out, and_20_out);
  or or_5 (g, and_27_out, and_28_out, and_29_out, and_30_out, and_31_out);
  or or_6 (d, and_12_out, and_13_out, and_14_out, and_15_out, and_16_out, and_17_out);
  or or_7 (f, and_21_out, and_22_out, and_23_out, and_24_out, and_25_out, and_26_out);
endmodule

module DigitosDezenas (
  input  Bit0,
  output a,
  output b,
  output c,
  output d,
  output e,
  output f
);

  not not_1 (a, Bit0);
  not not_2 (d, Bit0);
  not not_3 (e, Bit0);
  not not_4 (f, Bit0);

  assign b = 1'b1;
  assign c = 1'b1;
endmodule

module SelecionaDigitoDezena (
  input  Bit2,
  input  Bit1,
  input  Bit0,
  output a
);

  wire and_1_out, and_2_out;

  and and_1 (and_1_out, Bit2, Bit0);
  and and_2 (and_2_out, Bit2, Bit1);
  or or_1 (a, and_1_out, and_2_out);
endmodule
