// Logisim project DigitosDeZeroA999.circ as structural Verilog: 2 circuits, main circuit main
module main (
  input  Reverte_contagem,
  output out_2,
  output out_3,
  output out_4,
  output out_5,
  output out_6,
  output out_7,
  output out_8,
  output out_9,
  output out_10,
  output out_11,
  output out_12,
  output out_13
);

  wire clock_1_out, counter_3_carry, counter_4_carry, digitosunidades_1_a, digitosunidades_1_b,
       digitosunidades_1_c, digitosunidades_1_d, digitosunidades_1_e, digitosunidades_1_f,
       digitosunidades_1_g, digitosunidades_2_a, digitosunidades_2_b, digitosunidades_2_c,
       digitosunidades_2_d, digitosunidades_2_e, digitosunidades_2_f, digitosunidades_2_g,
       digitosunidades_3_a, digitosunidades_3_b, digitosunidades_3_c, digitosunidades_3_d,
       digitosunidades_3_e, digitosunidades_3_f, digitosunidades_3_g, Reinicia_contagem_out;
  wire [3:0] counter_2_q, counter_3_q, counter_4_q;

  Button Reinicia_contagem (.out(Reinicia_contagem_out));
  Clock clock_1 (.out(clock_1_out));
  Counter #(.width(12), .max('hfff)) counter_1 (
    .load(Reverte_contagem),
    .Q({out_2, out_3, out_4, out_5, out_6, out_7, out_8, out_9, out_10, out_11, out_12, out_13}),
    .clk(clock_1_out), .clr(Reinicia_contagem_out));  // open: D, count, carry
  Counter #(.width(4), .max('h9), .trigger("falling")) counter_2 (
    .load(Reverte_contagem), .Q(counter_2_q), .clk(counter_3_carry), .clr(Reinicia_contagem_out));  // open: D, count, carry
  Counter #(.width(4), .max('h9), .trigger("falling")) counter_3 (
    .load(Reverte_contagem), .Q(counter_3_q), .carry(counter_3_carry), .clk(counter_4_carry),
    .clr(Reinicia_contagem_out));  // open: D, count
  Counter #(.width(4), .max('h9), .trigger("falling")) counter_4 (
    .load(Reverte_contagem), .Q(counter_4_q), .carry(counter_4_carry), .clk(clock_1_out),
    .clr(Reinicia_contagem_out));  // open: D, count
  DigitosUnidades digitosunidades_1 (
    .Bit3(counter_2_q[3]), .Bit2(counter_2_q[2]), .Bit1(counter_2_q[1]), .Bit0(counter_2_q[0]),
    .a(digitosunidades_1_a), .b(digitosunidades_1_b), .c(digitosunidades_1_c), .d(digitosunidades_1_d),
    .e(digitosunidades_1_e), .f(digitosunidades_1_f), .g(digitosunidades_1_g));
  DigitosUnidades digitosunidades_2 (
    .Bit3(counter_3_q[3]), .Bit2(counter_3_q[2]), .Bit1(counter_3_q[1]), .Bit0(counter_3_q[0]),
    .a(digitosunidades_2_a), .b(digitosunidades_2_b), .c(digitosunidades_2_c), .d(digitosunidades_2_d),
    .e(digitosunidades_2_e), .f(digitosunidades_2_f), .g(digitosunidades_2_g));
  _7_Segment_Display u_7_segment_display_1 (
    .g(digitosunidades_1_g), .f(digitosunidades_1_f), .a(digitosunidades_1_a), .b(digitosunidades_1_b),
    .e(digitosunidades_1_e), .d(digitosunidades_1_d), .c(digitosunidades_1_c));  // open: dp
  _7_Segment_Display u_7_segment_display_2 (
    .g(digitosunidades_2_g), .f(digitosunidades_2_f), .a(digitosunidades_2_a), .b(digitosunidades_2_b),
    .e(digitosunidades_2_e), .d(digitosunidades_2_d), .c(digitosunidades_2_c));  // open: dp
  _7_Segment_Display u_7_segment_display_3 (
    .g(digitosunidades_3_g), .f(digitosunidades_3_f), .a(digitosunidades_3_a), .b(digitosunidades_3_b),
    .e(digitosunidades_3_e), .d(digitosunidades_3_d), .c(digitosunidades_3_c));  // open: dp
  DigitosUnidades digitosunidades_3 (
    .Bit3(counter_4_q[3]), .Bit2(counter_4_q[2]), .Bit1(counter_4_q[1]), .Bit0(counter_4_q[0]),
    .a(digitosunidades_3_a), .b(digitosunidades_3_b), .c(digitosunidades_3_c), .d(digitosunidades_3_d),
    .e(digitosunidades_3_e), .f(digitosunidades_3_f), .g(digitosunidades_3_g));
endmodule

module DigitosUnidades (
  input  Bit3,
  input  Bit2,
  input  Bit1,
  input  Bit0,
  output a,
  output b,
  output c,
  output d,
  output e,
  output f,
  output g
);

  wire and_1_out, and_2_out, and_3_out, and_4_out, and_5_out, and_6_out, and_7_out, and_8_out, and_9_out,
       and_10_out, and_11_out, and_12_out, and_13_out, and_14_out, and_15_out, and_16_out, and_17_out,
       and_18_out, and_19_out, and_20_out, and_21_out, and_22_out, and_23_out, and_24_out, and_25_out,
       and_26_out, and_27_out, and_28_out, and_29_out, and_30_out, and_31_out, not_1_out, not_2_out,
       not_3_out, not_4_out, not_5_out, not_6_out, not_7_out, not_8_out, not_9_out, not_10_out, not_11_out,
       not_12_out, not_13_out, not_14_out, not_15_out, not_16_out, not_17_out, not_18_out, not_19_out,
       not_20_out, not_21_out, not_22_out, not_23_out, not_24_out, not_25_out, not_26_out, not_27_out,
       not_28_out, not_29_out, not_30_out, not_31_out, not_32_out, not_33_out, not_34_out, not_35_out,
       not_36_out, not_37_out, not_38_out, not_39_out, not_40_out, not_41_out, not_42_out, not_43_out,
       not_44_out;

  not not_1 (not_1_out, Bit2);
  and and_1 (and_1_out, not_1_out, not_2_out);
  not not_2 (not_2_out, Bit0);
  not not_3 (not_3_out, Bit3);
  and and_2 (and_2_out, not_3_out, Bit1);
  and and_3 (and_3_out, Bit2, Bit0);
  and and_4 (and_4_out, Bit3, not_4_out);
  not not_4 (not_4_out, Bit1);
  not not_5 (not_5_out, Bit2);
  not not_6 (not_6_out, Bit1);
  and and_5 (and_5_out, not_6_out, not_7_out);
  not not_7 (not_7_out, Bit0);
  not not_8 (not_8_out, Bit3);
  and and_6 (and_6_out, not_8_out, Bit1, Bit0);
  and and_7 (and_7_out, Bit3, not_9_out);
  not not_9 (not_9_out, Bit1);
  and and_8 (and_8_out, Bit3, not_10_out);
  not not_10 (not_10_out, Bit0);
  not not_11 (not_11_out, Bit3);
  and and_9 (and_9_out, not_11_out, not_12_out);
  not not_12 (not_12_out, Bit1);
  and and_10 (and_10_out, Bit2, Bit1);
  and and_11 (and_11_out, Bit3, not_13_out);
  not not_13 (not_13_out, Bit2);
  not not_14 (not_14_out, Bit2);
  and and_12 (and_12_out, not_14_out, not_15_out);
  not not_15 (not_15_out, Bit0);
  not not_16 (not_16_out, Bit3);
  and and_13 (and_13_out, not_16_out, not_17_out, Bit1);
  not not_17 (not_17_out, Bit2);
  not not_18 (not_18_out, Bit3);
  and and_14 (and_14_out, not_18_out, Bit1, not_19_out);
  not not_19 (not_19_out, Bit0);
  not not_20 (not_20_out, Bit1);
  and and_15 (and_15_out, Bit2, not_20_out, Bit0);
  not not_21 (not_21_out, Bit1);
  and and_16 (and_16_out, Bit3, not_21_out, not_22_out);
  not not_22 (not_22_out, Bit0);
  and and_17 (and_17_out, Bit3, Bit2, Bit0);
  not not_23 (not_23_out, Bit2);
  and and_18 (and_18_out, not_23_out, not_24_out);
  not not_24 (not_24_out, Bit0);
  not not_25 (not_25_out, Bit3);
  and and_19 (and_19_out, not_25_out, Bit1, not_26_out);
  not not_26 (not_26_out, Bit0);
  and and_20 (and_20_out, Bit3, not_27_out, not_28_out);
  not not_27 (not_27_out, Bit1);
  not not_28 (not_28_out, Bit0);
  not not_29 (not_29_out, Bit3);
  not not_30 (not_30_out, Bit1);
  and and_21 (and_21_out, not_29_out, not_30_out, not_31_out);
  not not_31 (not_31_out, Bit0);
  not not_32 (not_32_out, Bit3);
  and and_22 (and_22_out, not_32_out, Bit2, not_33_out);
  not not_33 (not_33_out, Bit1);
  not not_34 (not_34_out, Bit3);
  and and_23 (and_23_out, not_34_out, Bit2, not_35_out);
  not not_35 (not_35_out, Bit0);
  and and_24 (and_24_out, Bit3, not_36_out, not_37_out);
  not not_36 (not_36_out, Bit2);
  not not_37 (not_37_out, Bit1);
  and and_25 (and_25_out, Bit3, not_38_out, not_39_out);
  not not_38 (not_38_out, Bit2);
  not not_39 (not_39_out, Bit0);
  and and_26 (and_26_out, Bit3, Bit2, Bit1);
  not not_40 (not_40_out, Bit3);
  and and_27 (and_27_out, not_40_out, not_41_out, Bit1);
  not not_41 (not_41_out, Bit2);
  and and_28 (and_28_out, Bit2, not_42_out);
  not not_42 (not_42_out, Bit1);
  and and_29 (and_29_out, Bit2, not_43_out);
  not not_43 (not_43_out, Bit0);
  and and_30 (and_30_out, Bit3, not_44_out);
  not not_44 (not_44_out, Bit1);
  and and_31 (and_31_out, Bit3, Bit2);
  or or_1 (a, and_1_out, and_2_out, and_3_out, and_4_out);
  or or_2 (b, not_5_out, and_5_out, and_6_out, and_7_out, and_8_out);
  or or_3 (c, and_9_out, Bit0, and_10_out, and_11_out);
  or or_4 (e, and_18_out, and_19_out, and_20_out);
  or or_5 (g, and_27_out, and_28_out, and_29_out, and_30_out, and_31_out);
  or or_6 (d, and_12_out, and_13_out, and_14_out, and_15_out, and_16_out, and_17_out);
  or or_7 (f, and_21_out, and_22_out, and_23_out, and_24_out, and_25_out, and_26_out);
endmodule
