// Logisim project DigitosImpares1a15.circ as structural Verilog: 4 circuits, main circuit DigitosUnidades
module main (
  input  in_1,
  output out_2,
  output out_3,
  output out_4
);

  wire clock_1_out, digitosdezenas_1_a, digitosdezenas_1_b, digitosdezenas_1_c, digitosdezenas_1_d,
       digitosdezenas_1_e, digitosdezenas_1_f, digitosunidades_1_a, digitosunidades_1_b, digitosunidades_1_c,
       digitosunidades_1_d, digitosunidades_1_e, digitosunidades_1_f, digitosunidades_1_g,
       selecionadigitodezena_1_a;

  Clock #(.highDuration(5)) clock_1 (.out(clock_1_out));
  Counter #(.width(3), .max('h7)) counter_1 (
    .count(in_1), .Q({out_2, out_3, out_4}), .clk(clock_1_out));  // open: load, D, carry, clr
  SelecionaDigitoDezena selecionadigitodezena_1 (
    .Bit2(out_2), .Bit1(out_3), .Bit0(out_4), .a(selecionadigitodezena_1_a));
  DigitosDezenas digitosdezenas_1 (
    .Bit0(selecionadigitodezena_1_a), .a(digitosdezenas_1_a), .b(digitosdezenas_1_b), .c(digitosdezenas_1_c),
    .d(digitosdezenas_1_d), .e(digitosdezenas_1_e), .f(digitosdezenas_1_f));
  _7_Segment_Display u_7_segment_display_1 (
    .f(digitosdezenas_1_f), .a(digitosdezenas_1_a), .b(digitosdezenas_1_b), .e(digitosdezenas_1_e),
    .d(digitosdezenas_1_d), .c(digitosdezenas_1_c));  // open: g, dp
  _7_Segment_Display u_7_segment_display_2 (
    .g(digitosunidades_1_g), .f(digitosunidades_1_f), .a(digitosunidades_1_a), .b(digitosunidades_1_b),
    .e(digitosunidades_1_e), .d(digitosunidades_1_d), .c(digitosunidades_1_c));  // open: dp
  DigitosUnidades digitosunidades_1 (
    .Bit2(out_2), .Bit1(out_3), .Bit0(out_4), .a(digitosunidades_1_a), .b(digitosunidades_1_b),
    .c(digitosunidades_1_c), .d(digitosunidades_1_d), .e(digitosunidades_1_e), .f(digitosunidades_1_f),
    .g(digitosunidades_1_g));
endmodule

module DigitosUnidades (
  input  Bit2,
  input  Bit1,
  input  Bit0,
  output a,
  output b,
  output c,
  output d,
  output e,
  output f,
  output g
);

  wire and_1_out, and_2_out, and_3_out, and_4_out, and_5_out, and_6_out, and_7_out, and_8_out, and_9_out,
       and_10_out, and_11_out, and_12_out, and_13_out, and_14_out, not_1_out, not_2_out, not_3_out,
       not_4_out, not_5_out, not_6_out, not_7_out, not_8_out, not_9_out, not_10_out, not_11_out, not_12_out,
       not_13_out, not_14_out, not_15_out, not_16_out;

  not not_1 (not_1_out, Bit2);
  not not_2 (not_2_out, Bit0);
  not not_3 (not_3_out, Bit2);
  not not_4 (not_4_out, Bit0);
  not not_5 (not_5_out, Bit2);
  not not_6 (not_6_out, Bit1);
  not not_7 (not_7_out, Bit0);
  not not_8 (not_8_out, Bit2);
  not not_9 (not_9_out, Bit0);
  not not_10 (not_10_out, Bit1);
  not not_11 (not_11_out, Bit0);
  not not_12 (not_12_out, Bit2);
  not not_13 (not_13_out, Bit1);
  not not_14 (not_14_out, Bit0);
  not not_15 (not_15_out, Bit0);
  and and_1 (and_1_out, not_1_out, Bit0);
  and and_2 (and_2_out, Bit2, not_2_out);
  not not_16 (not_16_out, Bit1);
  and and_3 (and_3_out, not_3_out, Bit0);
  and and_4 (and_4_out, Bit2, not_4_out);
  and and_5 (and_5_out, not_5_out, not_6_out, Bit0);
  and and_6 (and_6_out, Bit1, not_7_out);
  and and_7 (and_7_out, Bit2, Bit1);
  and and_8 (and_8_out, not_8_out, Bit1, not_9_out);
  and and_9 (and_9_out, Bit2, not_10_out, not_11_out);
  and and_10 (and_10_out, Bit2, Bit1, Bit0);
  and and_11 (and_11_out, not_12_out, not_13_out, Bit0);
  and and_12 (and_12_out, Bit1, not_14_out);
  and and_13 (and_13_out, Bit2, not_15_out);
  and and_14 (and_14_out, Bit2, Bit1);
  or or_1 (a, and_1_out, Bit1, and_2_out);
  or or_2 (b, not_16_out, and_3_out, and_4_out);
  or or_3 (d, and_5_out, and_6_out, and_7_out);
  or or_4 (f, and_8_out, and_9_out, and_10_out);
  or or_5 (g, and_11_out, and_12_out, and_13_out, and_14_out);

  assign c = 1'b1;
  assign e = 1'b0;
endmodule

module DigitosDezenas (
  input  Bit0,
  output a,
  output b,
  output c,
  output d,
  output e,
  output f
);

  not not_1 (a, Bit0);
  not not_2 (d, Bit0);
  not not_3 (e, Bit0);
  not not_4 (f, Bit0);

  assign b = 1'b1;
  assign c = 1'b1;
endmodule

module SelecionaDigitoDezena (
  input  Bit2,
  input  Bit1,
  input  Bit0,
  output a
);

  wire and_1_out, and_2_out;

  and and_1 (and_1_out, Bit2, Bit0);
  and and_2 (and_2_out, Bit2, Bit1);
  or or_1 (a, and_1_out, and_2_out);
endmodule
