// Logisim project Display de sete segmentos.circ as structural Verilog: 1 circuit, main circuit main
module main (
  input  in_1,
  input  in_2,
  output out_3,
  output A,
  output B,
  output C,
  output D,
  output out_8,
  output out_9,
  output out_10,
  output out_11
);

  wire a_out, and_1_out, and_2_out, and_3_out, and_4_out, and_5_out, and_6_out, and_7_out, and_8_out,
       and_9_out, and_10_out, and_11_out, and_12_out, and_13_out, and_14_out, and_15_out, and_16_out,
       and_17_out, b_out, c_out, d_out, e_out, f_out, g_out, not_1_out, not_2_out, not_3_out, not_4_out,
       not_5_out, not_6_out, not_7_out, not_8_out, not_9_out, not_10_out, not_11_out, not_12_out, not_13_out,
       not_14_out, not_15_out, not_16_out, not_17_out, not_18_out, not_19_out, not_20_out, not_21_out,
       not_22_out, not_23_out, not_24_out;
  wire [3:0] undriven;

  not not_1 (not_1_out, B);
  not not_2 (not_2_out, C);
  not not_3 (not_3_out, D);
  not not_4 (not_4_out, C);
  not not_5 (not_5_out, D);
  not not_6 (not_6_out, B);
  not not_7 (not_7_out, C);
  not not_8 (not_8_out, B);
  not not_9 (not_9_out, D);
  not not_10 (not_10_out, B);
  not not_11 (not_11_out, D);
  not not_12 (not_12_out, B);
  not not_13 (not_13_out, C);
  not not_14 (not_14_out, B);
  not not_15 (not_15_out, C);
  not not_16 (not_16_out, D);
  not not_17 (not_17_out, D);
  not not_18 (not_18_out, C);
  not not_19 (not_19_out, D);
  not not_20 (not_20_out, C);
  not not_21 (not_21_out, D);
  not not_22 (not_22_out, C);
  not not_23 (not_23_out, B);
  not not_24 (not_24_out, D);
  and and_1 (and_1_out, B, D);
  and and_2 (and_2_out, not_1_out, not_2_out, not_3_out);
  and and_3 (and_3_out, not_4_out, not_5_out);
  and and_4 (and_4_out, C, D);
  and and_5 (and_5_out, not_8_out, not_9_out);
  and and_6 (and_6_out, not_10_out, C);
  and and_7 (and_7_out, C, not_11_out);
  and and_8 (and_8_out, A, not_12_out);
  and and_9 (and_9_out, B, B, not_13_out, D);
  and and_10 (and_10_out, not_14_out, not_15_out, not_16_out);
  and and_11 (and_11_out, C, not_17_out);
  and and_12 (and_12_out, not_18_out, not_19_out);
  and and_13 (and_13_out, B, B, B, not_20_out);
  and and_14 (and_14_out, B, B, not_21_out);
  and and_15 (and_15_out, B, not_22_out);
  and and_16 (and_16_out, not_23_out, C, C);
  and and_17 (and_17_out, C, not_24_out);
  or u_a (a_out, A, C, and_2_out, and_1_out);
  or u_b (b_out, and_3_out, and_4_out, not_6_out);
  or u_c (c_out, not_7_out, B, D);
  or u_d (d_out, and_5_out, and_6_out, and_7_out, and_8_out, and_9_out);
  or e (e_out, and_10_out, and_11_out);
  or f (f_out, and_12_out, and_13_out, and_14_out, A);
  or g (g_out, and_15_out, and_16_out, and_17_out, A);
  _7_Segment_Display u_7_segment_display_1 (
    .g(g_out), .f(f_out), .a(a_out), .b(b_out), .e(e_out), .d(d_out), .c(c_out));  // open: dp
  Counter #(.width(4), .max('h9), .trigger("falling")) counter_1 (
    .load(in_1), .D(undriven), .Q({A, B, C, D}), .clk(out_11), .clr(in_2));  // open: count, carry
  Clock #(.highDuration(3), .lowDuration(3)) clock_1 (.out(out_11));

  assign out_3 = D;
  assign out_8 = C;
  assign out_9 = B;
  assign out_10 = A;
endmodule
