// Logisim project DisplayRCS.circ as structural Verilog: 2 circuits, main circuit ControlaSegmentos
module Principal (
  input  in_1,
  input  in_2,
  output out_3,
  output out_4,
  output out_5,
  output out_6,
  output out_7,
  output out_8,
  output out_9
);

  wire and_1_out, button_1_out, clock_1_out, or_1_out;
  wire [7:0] counter_1_q;

  _7_Segment_Display u_7_segment_display_1 (
    .g(out_9), .f(out_8), .a(out_3), .b(out_4), .e(out_7), .d(out_6), .c(out_5));  // open: dp
  LED led_1 (.in(counter_1_q[1]));
  LED led_2 (.in(counter_1_q[0]));
  ControlaSegmentos controlasegmentos_1 (
    .A(counter_1_q[1]), .B(counter_1_q[0]), .a_2(out_3), .b_2(out_4), .c(out_5), .d(out_6), .e(out_7),
    .f(out_8), .g(out_9));
  or or_1 (or_1_out, button_1_out, and_1_out);
  Button button_1 (.out(button_1_out));
  Counter counter_1 (.load(in_1), .Q(counter_1_q), .clk(or_1_out));  // open: D, count, carry, clr
  and and_1 (and_1_out, clock_1_out, in_2);
  Clock clock_1 (.out(clock_1_out));
endmodule

module ControlaSegmentos (
  input  A,
  input  B,
  output a_2,
  output b_2,
  output c,
  output d,
  output e,
  output f,
  output g
);

  wire and_2_out, and_3_out, not_1_out, not_2_out, not_3_out;

  or or_1 (a_2, B, A);
  not not_1 (not_1_out, A);
  not not_2 (not_2_out, A);
  not not_3 (not_3_out, B);
  or or_2 (f, B, A);
  and and_1 (b_2, not_1_out, B);
  and and_2 (and_2_out, not_2_out, B);
  and and_3 (and_3_out, A, not_3_out);
  or or_3 (e, and_2_out, and_3_out);

  assign c = B;
  assign d = A;
  assign g = B;
endmodule
