// Logisim project DisplayRCS2.circ as structural Verilog: 2 circuits, main circuit Principal-main
module Principal_main (
  input  in_1,
  input  in_2
);

  wire and_1_out, button_1_out, ci_controlesegmentos_1_a_2, ci_controlesegmentos_1_b_2,
       ci_controlesegmentos_1_c, ci_controlesegmentos_1_d, ci_controlesegmentos_1_e,
       ci_controlesegmentos_1_f, ci_controlesegmentos_1_g, clock_1_out, or_1_out;
  wire [1:0] counter_1_q;

  Button button_1 (.out(button_1_out));
  Clock clock_1 (.out(clock_1_out));
  and and_1 (and_1_out, clock_1_out, in_2);
  Counter #(.width(2), .max('h3), .trigger("falling")) counter_1 (
    .load(in_1), .Q(counter_1_q), .clk(or_1_out));  // open: D, count, carry, clr
  or or_1 (or_1_out, button_1_out, and_1_out);
  CI_ControleSegmentos ci_controlesegmentos_1 (
    .A(counter_1_q[1]), .B(counter_1_q[0]), .a_2(ci_controlesegmentos_1_a_2),
    .b_2(ci_controlesegmentos_1_b_2), .c(ci_controlesegmentos_1_c), .d(ci_controlesegmentos_1_d),
    .e(ci_controlesegmentos_1_e), .f(ci_controlesegmentos_1_f), .g(ci_controlesegmentos_1_g));
  _7_Segment_Display u_7_segment_display_1 (
    .g(ci_controlesegmentos_1_g), .f(ci_controlesegmentos_1_f), .a(ci_controlesegmentos_1_a_2),
    .b(ci_controlesegmentos_1_b_2), .e(ci_controlesegmentos_1_e), .d(ci_controlesegmentos_1_d),
    .c(ci_controlesegmentos_1_c));  // open: dp
endmodule

module CI_ControleSegmentos (
  input  A,
  input  B,
  output a_2,
  output b_2,
  output c,
  output d,
  output e,
  output f,
  output g
);

  wire and_2_out, and_3_out, not_1_out, not_2_out;

  and and_1 (c, A, B);
  not not_1 (not_1_out, A);
  not not_2 (not_2_out, B);
  and and_2 (and_2_out, not_1_out, B);
  and and_3 (and_3_out, A, not_2_out);
  or or_1 (e, and_2_out, and_3_out);

  assign a_2 = A;
  assign b_2 = 1'b0;
  assign d = A;
  assign f = A;
  assign g = B;
endmodule
