// Logisim project DoisDisplaysSeteSegmentos.circ as structural Verilog: 3 circuits, main circuit DoisDisplaysSeteSegmentos
module DoisDisplaysSeteSegmentos (
  input  Ligado__On,
  input  Decrementa,
  input  in_3
);

  wire and_1_out, clock_1_out, controlecontagem_1_a, controlecontagem_1_b, controlecontagem_1_c,
       controlecontagem_1_d, controlecontagem_1_da, controlecontagem_1_db, controlecontagem_1_dc,
       controlecontagem_1_dd, controlecontagem_1_de, controlecontagem_1_df, controlecontagem_1_dg,
       controlecontagem_1_e, controlecontagem_1_f, controlecontagem_1_g, or_1_out, Passo_out, Reiniciar_out;

  Button Passo (.out(Passo_out));
  Clock clock_1 (.out(clock_1_out));
  and and_1 (and_1_out, clock_1_out, in_3);
  or or_1 (or_1_out, Passo_out, and_1_out);
  Button Reiniciar (.out(Reiniciar_out));
  ControleContagem controlecontagem_1 (
    .ON(Ligado__On), .Decrementa(Decrementa), .UmPasso(or_1_out), .Reiniciar(Reiniciar_out),
    .Da(controlecontagem_1_da), .Db(controlecontagem_1_db), .Dc(controlecontagem_1_dc),
    .Dd(controlecontagem_1_dd), .De(controlecontagem_1_de), .Df(controlecontagem_1_df),
    .Dg(controlecontagem_1_dg), .a(controlecontagem_1_a), .b(controlecontagem_1_b), .c(controlecontagem_1_c),
    .d(controlecontagem_1_d), .e(controlecontagem_1_e), .f(controlecontagem_1_f), .g(controlecontagem_1_g));
  _7_Segment_Display u_7_segment_display_1 (
    .g(controlecontagem_1_dg), .f(controlecontagem_1_df), .a(controlecontagem_1_da),
    .b(controlecontagem_1_db), .e(controlecontagem_1_de), .d(controlecontagem_1_dd), .c(controlecontagem_1_dc));  // open: dp
  _7_Segment_Display u_7_segment_display_2 (
    .g(controlecontagem_1_g), .f(controlecontagem_1_f), .a(controlecontagem_1_a), .b(controlecontagem_1_b),
    .e(controlecontagem_1_e), .d(controlecontagem_1_d), .c(controlecontagem_1_c));  // open: dp
endmodule

// Controle de Contagem
module ControleContagem (
  input  ON,
  input  Decrementa,
  input  UmPasso,
  input  Reiniciar,
  output Da,
  output Db,
  output Dc,
  output Dd,
  output De,
  output Df,
  output Dg,
  output a,
  output b,
  output c,
  output d,
  output e,
  output f,
  output g
);

  wire counter_2_carry;
  wire [7:0] counter_1_q, counter_2_q;

  Counter #(.max('h9), .ongoal("stay"), .trigger("falling")) counter_1 (
    .load(Decrementa), .Q(counter_1_q), .clk(counter_2_carry), .clr(Reiniciar));  // open: D, count, carry
  MapeiaDigitos mapeiadigitos_1 (
    .On(ON), .A(counter_1_q[3]), .B(counter_1_q[2]), .C(counter_1_q[1]), .D(counter_1_q[0]), .a_2(Da),
    .b_2(Db), .c_2(Dc), .d_2(Dd), .e(De), .f(Df), .g(Dg));
  Counter #(.max('h9), .ongoal("load")) counter_2 (
    .load(Decrementa), .Q(counter_2_q), .carry(counter_2_carry), .clk(UmPasso), .clr(Reiniciar));  // open: D, count
  MapeiaDigitos mapeiadigitos_2 (
    .On(ON), .A(counter_2_q[3]), .B(counter_2_q[2]), .C(counter_2_q[1]), .D(counter_2_q[0]), .a_2(a),
    .b_2(b), .c_2(c), .d_2(d), .e(e), .f(f), .g(g));
endmodule

module MapeiaDigitos (
  input  On,
  input  A,
  input  B,
  input  C,
  input  D,
  output a_2,
  output b_2,
  output c_2,
  output d_2,
  output e,
  output f,
  output g
);

  wire and_1_out, and_2_out, and_3_out, and_4_out, and_5_out, and_6_out, and_7_out, and_8_out, and_9_out,
       and_10_out, and_11_out, and_12_out, and_13_out, and_14_out, and_15_out, and_16_out, and_17_out,
       and_18_out, and_19_out, and_20_out, and_21_out, and_22_out, and_23_out, and_24_out, and_25_out,
       and_26_out, not_1_out, not_2_out, not_3_out, not_4_out, not_5_out, not_6_out, not_7_out, not_8_out,
       not_9_out, not_10_out, not_11_out, not_12_out, not_13_out, not_14_out, not_15_out, not_16_out,
       not_17_out, not_18_out, not_19_out, not_20_out, not_21_out, not_22_out, not_23_out, not_24_out,
       not_25_out, not_26_out, not_27_out, not_28_out, not_29_out, not_30_out, not_31_out, not_32_out,
       not_33_out, not_34_out, not_35_out, not_36_out, not_37_out, not_38_out, not_39_out, not_40_out,
       not_41_out, not_42_out, not_43_out, not_44_out, not_45_out, not_46_out, not_47_out, not_48_out,
       not_49_out, not_50_out, not_51_out, not_52_out;

  not not_1 (not_1_out, A);
  not not_2 (not_2_out, B);
  not not_3 (not_3_out, D);
  not not_4 (not_4_out, A);
  not not_5 (not_5_out, A);
  not not_6 (not_6_out, B);
  not not_7 (not_7_out, C);
  not not_8 (not_8_out, A);
  not not_9 (not_9_out, B);
  not not_10 (not_10_out, A);
  not not_11 (not_11_out, C);
  not not_12 (not_12_out, D);
  not not_13 (not_13_out, B);
  not not_14 (not_14_out, C);
  not not_15 (not_15_out, A);
  not not_16 (not_16_out, B);
  not not_17 (not_17_out, C);
  not not_18 (not_18_out, A);
  not not_19 (not_19_out, A);
  not not_20 (not_20_out, A);
  not not_21 (not_21_out, B);
  not not_22 (not_22_out, D);
  not not_23 (not_23_out, A);
  not not_24 (not_24_out, B);
  not not_25 (not_25_out, A);
  not not_26 (not_26_out, D);
  not not_27 (not_27_out, A);
  not not_28 (not_28_out, C);
  not not_29 (not_29_out, B);
  not not_30 (not_30_out, C);
  not not_31 (not_31_out, B);
  not not_32 (not_32_out, C);
  not not_33 (not_33_out, D);
  not not_34 (not_34_out, A);
  not not_35 (not_35_out, D);
  not not_36 (not_36_out, A);
  not not_37 (not_37_out, C);
  not not_38 (not_38_out, D);
  not not_39 (not_39_out, A);
  not not_40 (not_40_out, C);
  not not_41 (not_41_out, A);
  not not_42 (not_42_out, D);
  not not_43 (not_43_out, B);
  not not_44 (not_44_out, C);
  not not_45 (not_45_out, A);
  not not_46 (not_46_out, B);
  not not_47 (not_47_out, A);
  not not_48 (not_48_out, C);
  not not_49 (not_49_out, A);
  not not_50 (not_50_out, D);
  not not_51 (not_51_out, B);
  not not_52 (not_52_out, C);
  and and_1 (and_1_out, On, not_1_out, not_2_out, not_3_out);
  and and_2 (and_2_out, On, not_4_out, C);
  and and_3 (and_3_out, On, not_5_out, B, D);
  and and_4 (and_4_out, On, A, not_6_out, not_7_out);
  and and_5 (and_5_out, On, not_8_out, not_9_out);
  and and_6 (and_6_out, On, not_10_out, not_11_out, not_12_out);
  and and_7 (and_7_out, On, not_13_out, not_14_out);
  and and_8 (and_8_out, On, not_15_out, C, D);
  and and_9 (and_9_out, On, not_16_out, not_17_out);
  and and_10 (and_10_out, On, not_18_out, D);
  and and_11 (and_11_out, On, not_19_out, B);
  and and_12 (and_12_out, On, not_20_out, not_21_out, not_22_out);
  and and_13 (and_13_out, On, not_23_out, not_24_out, C);
  and and_14 (and_14_out, On, not_25_out, C, not_26_out);
  and and_15 (and_15_out, On, not_27_out, B, not_28_out, D);
  and and_16 (and_16_out, On, A, not_29_out, not_30_out);
  and and_17 (and_17_out, On, not_31_out, not_32_out, not_33_out);
  and and_18 (and_18_out, On, not_34_out, C, not_35_out);
  and and_19 (and_19_out, On, not_36_out, not_37_out, not_38_out);
  and and_20 (and_20_out, On, not_39_out, B, not_40_out);
  and and_21 (and_21_out, On, not_41_out, B, not_42_out);
  and and_22 (and_22_out, On, A, not_43_out, not_44_out);
  and and_23 (and_23_out, On, not_45_out, not_46_out, C);
  and and_24 (and_24_out, On, not_47_out, B, not_48_out);
  and and_25 (and_25_out, On, not_49_out, B, not_50_out);
  and and_26 (and_26_out, On, A, not_51_out, not_52_out);
  or or_1 (a_2, and_1_out, and_2_out, and_3_out, and_4_out);
  or or_2 (b_2, and_5_out, and_6_out, and_7_out, and_8_out);
  or or_3 (c_2, and_9_out, and_10_out, and_11_out);
  or or_4 (d_2, and_12_out, and_13_out, and_14_out, and_15_out, and_16_out);
  or or_5 (e, and_17_out, and_18_out);
  or or_6 (f, and_19_out, and_20_out, and_21_out, and_22_out);
  or or_7 (g, and_23_out, and_24_out, and_25_out, and_26_out);
endmodule
