// Logisim project I_like_sistematologica.circ as structural Verilog: 6 circuits, main circuit Main
// Principal
module Main (
  input  in_1,
  input  in_2,
  input  in_3
);

  wire a_2_out, a_g_1_a, a_g_1_b, a_g_1_c, a_g_1_d, a_g_1_e, a_g_1_f, a_g_1_g, and_1_out, b_2_out,
       button_1_out, c_2_out, clock_1_out, d_2_out, e_2_out, f_out, g_2_out, h_o_1_a, h_o_1_b, h_o_1_c,
       h_o_1_d, h_o_1_e, h_o_1_f, h_o_1_g, keyboard_1_avail, or_1_out, p_w_1_a, p_w_1_b, p_w_1_c, p_w_1_d,
       p_w_1_e, p_w_1_f, p_w_1_g, Ponto_out, seteparacincobits_1_a_g, seteparacincobits_1_bit_0,
       seteparacincobits_1_bit_1, seteparacincobits_1_bit_2, seteparacincobits_1_i_p,
       seteparacincobits_1_q_x, seteparacincobits_1_y_z, \x_y_z_espaço_1_a , \x_y_z_espaço_1_b ,
       \x_y_z_espaço_1_c , \x_y_z_espaço_1_d , \x_y_z_espaço_1_e , \x_y_z_espaço_1_f , \x_y_z_espaço_1_g ;
  wire [6:0] keyboard_1_data;

  Button button_1 (.out(button_1_out));
  Clock clock_1 (.out(clock_1_out));
  and and_1 (and_1_out, clock_1_out, in_1);
  Keyboard #(.buflen(128), .trigger("falling")) keyboard_1 (
    .clk(or_1_out), .re(in_3), .clr(in_2), .avail(keyboard_1_avail), .data(keyboard_1_data));
  or or_1 (or_1_out, button_1_out, and_1_out);
  LED led_1 (.in(keyboard_1_avail));
  SeteParaCincoBits seteparacincobits_1 (
    .Entrada_de_sete_bits(keyboard_1_data), .A_G(seteparacincobits_1_a_g), .I_P(seteparacincobits_1_i_p),
    .Q_X(seteparacincobits_1_q_x), .Y_Z(seteparacincobits_1_y_z), .Bit_2(seteparacincobits_1_bit_2),
    .Bit_1(seteparacincobits_1_bit_1), .Bit_0(seteparacincobits_1_bit_0));
  A_G a_g_1 (
    .On(seteparacincobits_1_a_g), .Bit2(seteparacincobits_1_bit_2), .Bit1(seteparacincobits_1_bit_1),
    .Bit0(seteparacincobits_1_bit_0), .a(a_g_1_a), .b(a_g_1_b), .c(a_g_1_c), .d(a_g_1_d), .e(a_g_1_e),
    .f(a_g_1_f), .g(a_g_1_g));
  H_O h_o_1 (
    .On(seteparacincobits_1_i_p), .Bit2(seteparacincobits_1_bit_2), .Bit1(seteparacincobits_1_bit_1),
    .Bit0(seteparacincobits_1_bit_0), .a(h_o_1_a), .b(h_o_1_b), .c(h_o_1_c), .d(h_o_1_d), .e(h_o_1_e),
    .f(h_o_1_f), .g(h_o_1_g));
  P_W p_w_1 (
    .On(seteparacincobits_1_q_x), .Bit2(seteparacincobits_1_bit_2), .Bit1(seteparacincobits_1_bit_1),
    .Bit0(seteparacincobits_1_bit_0), .a(p_w_1_a), .b(p_w_1_b), .c(p_w_1_c), .d(p_w_1_d), .e(p_w_1_e),
    .f(p_w_1_f), .g(p_w_1_g));
  \X_Y_Z_espaço  \x_y_z_espaço_1  (
    .On(seteparacincobits_1_y_z), .Bit2(seteparacincobits_1_bit_2), .Bit1(seteparacincobits_1_bit_1),
    .Bit0(seteparacincobits_1_bit_0), .a(\x_y_z_espaço_1_a ), .b(\x_y_z_espaço_1_b ), .c(\x_y_z_espaço_1_c ),
    .d(\x_y_z_espaço_1_d ), .e(\x_y_z_espaço_1_e ), .f(\x_y_z_espaço_1_f ), .g(\x_y_z_espaço_1_g ));
  LED a (.in(a_2_out));
  or a_2 (a_2_out, a_g_1_a, h_o_1_a, p_w_1_a, \x_y_z_espaço_1_a );
  LED b (.in(b_2_out));
  or b_2 (b_2_out, a_g_1_b, h_o_1_b, p_w_1_b, \x_y_z_espaço_1_b );
  LED c (.in(c_2_out));
  or c_2 (c_2_out, a_g_1_c, h_o_1_c, p_w_1_c, \x_y_z_espaço_1_c );
  LED d (.in(d_2_out));
  or d_2 (d_2_out, a_g_1_d, h_o_1_d, p_w_1_d, \x_y_z_espaço_1_d );
  LED e (.in(e_2_out));
  or e_2 (e_2_out, a_g_1_e, h_o_1_e, p_w_1_e, \x_y_z_espaço_1_e );
  or f (f_out, a_g_1_f, h_o_1_f, p_w_1_f, \x_y_z_espaço_1_f );
  LED f_2 (.in(f_out));
  LED g (.in(g_2_out));
  or g_2 (g_2_out, a_g_1_g, h_o_1_g, p_w_1_g, \x_y_z_espaço_1_g );
  LED led_2 (.in(Ponto_out));
  // OR_Gate Ponto has open pins: out=Ponto_out
  _7_Segment_Display u_7_segment_display_1 (
    .g(g_2_out), .f(f_out), .a(a_2_out), .b(b_2_out), .e(e_2_out), .d(d_2_out), .c(c_2_out), .dp(Ponto_out));

  // Notes on the sheet:
  //   Circuito principal (main)
  //   Sistematologica
endmodule

module SeteParaCincoBits (
  input  [6:0] Entrada_de_sete_bits,
  output A_G,
  output I_P,
  output Q_X,
  output Y_Z,
  output Bit_2,
  output Bit_1,
  output Bit_0
);

  wire not_1_out, not_2_out, not_3_out, not_4_out;

  not not_1 (not_1_out, Entrada_de_sete_bits[3]);
  and SubCircuito_1 (A_G, not_1_out, not_2_out);
  not not_2 (not_2_out, Entrada_de_sete_bits[4]);
  and SubCircuito_2 (I_P, Entrada_de_sete_bits[3], not_3_out);
  not not_3 (not_3_out, Entrada_de_sete_bits[4]);
  not not_4 (not_4_out, Entrada_de_sete_bits[3]);
  and SubCircuito_3 (Q_X, not_4_out, Entrada_de_sete_bits[4]);
  and SubCircuito_4 (Y_Z, Entrada_de_sete_bits[3], Entrada_de_sete_bits[4]);

  assign Bit_0 = Entrada_de_sete_bits[0];
  assign Bit_1 = Entrada_de_sete_bits[1];
  assign Bit_2 = Entrada_de_sete_bits[2];
endmodule

module A_G (
  input  On,
  input  Bit2,
  input  Bit1,
  input  Bit0,
  output a,
  output b,
  output c,
  output d,
  output e,
  output f,
  output g
);

  wire and_1_out, and_2_out, and_3_out, and_4_out, and_5_out, and_6_out, and_7_out, and_8_out, and_9_out,
       and_10_out, and_11_out, and_12_out, and_13_out, and_14_out, and_15_out, and_16_out, and_17_out,
       and_18_out, and_19_out, not_1_out, not_2_out, not_3_out, not_4_out, not_5_out, not_6_out, not_7_out,
       not_8_out, not_9_out, not_10_out, not_11_out, not_12_out, not_13_out, not_14_out, not_15_out,
       not_16_out;

  and and_1 (and_1_out, On, Bit0);
  and and_2 (and_2_out, On, Bit2, Bit1);
  not not_1 (not_1_out, Bit2);
  not not_2 (not_2_out, Bit1);
  not not_3 (not_3_out, Bit1);
  not not_4 (not_4_out, Bit0);
  not not_5 (not_5_out, Bit2);
  not not_6 (not_6_out, Bit1);
  not not_7 (not_7_out, Bit2);
  not not_8 (not_8_out, Bit0);
  not not_9 (not_9_out, Bit1);
  not not_10 (not_10_out, Bit0);
  not not_11 (not_11_out, Bit2);
  and and_3 (and_3_out, On, not_11_out, not_12_out);
  not not_12 (not_12_out, Bit0);
  and and_4 (and_4_out, On, Bit1, Bit0);
  and and_5 (and_5_out, On, Bit2, not_13_out);
  not not_13 (not_13_out, Bit1);
  and and_6 (and_6_out, On, Bit0);
  and and_7 (and_7_out, On, Bit1);
  and and_8 (and_8_out, On, Bit2);
  and and_9 (and_9_out, On, Bit0);
  and and_10 (and_10_out, On, Bit1);
  not not_14 (not_14_out, Bit1);
  and and_11 (and_11_out, On, not_14_out, Bit0);
  and and_12 (and_12_out, On, Bit1, not_15_out);
  not not_15 (not_15_out, Bit0);
  and and_13 (and_13_out, On, Bit2, not_16_out);
  not not_16 (not_16_out, Bit1);
  or or_1 (a, and_1_out, and_2_out);
  and and_14 (and_14_out, On, not_1_out, not_2_out, Bit0);
  or or_2 (b, and_14_out, and_15_out);
  and and_15 (and_15_out, On, Bit2, not_3_out, not_4_out);
  and and_16 (and_16_out, On, not_5_out, not_6_out, Bit0);
  and and_17 (and_17_out, On, not_7_out, Bit1, not_8_out);
  and and_18 (and_18_out, On, Bit2, not_9_out, not_10_out);
  and and_19 (and_19_out, On, Bit2, Bit1, Bit0);
  or or_3 (d, and_3_out, and_4_out, and_5_out);
  or or_4 (e, and_6_out, and_7_out, and_8_out);
  or or_5 (f, and_9_out, and_10_out);
  or or_6 (g, and_11_out, and_12_out, and_13_out);
  or or_7 (c, and_16_out, and_17_out, and_18_out, and_19_out);
endmodule

module H_O (
  input  On,
  input  Bit2,
  input  Bit1,
  input  Bit0,
  output a,
  output b,
  output c,
  output d,
  output e,
  output f,
  output g
);

  wire and_2_out, and_3_out, and_4_out, and_5_out, and_6_out, and_7_out, and_8_out, and_9_out, and_10_out,
       and_11_out, and_12_out, and_13_out, and_14_out, and_15_out, and_16_out, and_17_out, and_18_out,
       not_1_out, not_2_out, not_3_out, not_4_out, not_5_out, not_6_out, not_7_out, not_8_out, not_9_out,
       not_10_out, not_11_out, not_12_out, not_13_out, not_14_out, not_15_out, not_16_out;

  and and_1 (a, On, Bit2, Bit0);
  not not_1 (not_1_out, Bit2);
  and and_2 (and_2_out, On, not_1_out, not_2_out);
  not not_2 (not_2_out, Bit0);
  not not_3 (not_3_out, Bit2);
  and and_3 (and_3_out, On, not_3_out, Bit1);
  and and_4 (and_4_out, On, Bit2, Bit0);
  not not_4 (not_4_out, Bit2);
  and and_5 (and_5_out, On, not_4_out, not_5_out);
  not not_5 (not_5_out, Bit0);
  and and_6 (and_6_out, On, Bit1, not_6_out);
  not not_6 (not_6_out, Bit0);
  and and_7 (and_7_out, On, Bit2, Bit0);
  not not_7 (not_7_out, Bit2);
  not not_8 (not_8_out, Bit1);
  not not_9 (not_9_out, Bit0);
  and and_8 (and_8_out, On, not_10_out);
  not not_10 (not_10_out, Bit1);
  and and_9 (and_9_out, On, Bit0);
  and and_10 (and_10_out, On, Bit2);
  and and_11 (and_11_out, On, not_11_out);
  not not_11 (not_11_out, Bit1);
  and and_12 (and_12_out, On, Bit0);
  not not_12 (not_12_out, Bit2);
  not not_13 (not_13_out, Bit1);
  not not_14 (not_14_out, Bit0);
  not not_15 (not_15_out, Bit2);
  not not_16 (not_16_out, Bit0);
  or or_1 (b, and_2_out, and_3_out, and_4_out);
  or or_2 (c, and_5_out, and_6_out, and_7_out);
  and and_13 (and_13_out, On, not_7_out, Bit1);
  or or_3 (d, and_13_out, and_14_out, and_15_out);
  and and_14 (and_14_out, On, Bit1, Bit0);
  and and_15 (and_15_out, On, Bit2, not_8_out, not_9_out);
  or or_4 (e, and_8_out, and_9_out, and_10_out);
  or or_5 (f, and_11_out, and_12_out);
  and and_16 (and_16_out, On, not_12_out, not_13_out, not_14_out);
  or or_6 (g, and_16_out, and_17_out, and_18_out);
  and and_17 (and_17_out, On, not_15_out, Bit1, Bit0);
  and and_18 (and_18_out, On, Bit2, Bit1, not_16_out);
endmodule

module P_W (
  input  On,
  input  Bit2,
  input  Bit1,
  input  Bit0,
  output a,
  output b,
  output c,
  output d,
  output e,
  output f,
  output g
);

  wire and_1_out, and_2_out, and_3_out, and_4_out, and_5_out, and_6_out, and_7_out, and_8_out, and_9_out,
       and_10_out, and_11_out, and_12_out, and_13_out, and_14_out, and_15_out, not_1_out, not_2_out,
       not_3_out, not_4_out, not_5_out, not_6_out, not_7_out, not_8_out, not_9_out, not_10_out, not_11_out,
       not_12_out, not_13_out, not_14_out;

  not not_1 (not_1_out, Bit2);
  and and_1 (and_1_out, On, not_1_out, not_2_out);
  not not_2 (not_2_out, Bit1);
  not not_3 (not_3_out, Bit2);
  and and_2 (and_2_out, On, not_3_out, Bit0);
  and and_3 (and_3_out, On, not_4_out, not_5_out);
  not not_4 (not_4_out, Bit2);
  not not_5 (not_5_out, Bit1);
  and and_4 (and_4_out, On, Bit2, Bit0);
  not not_6 (not_6_out, Bit2);
  not not_7 (not_7_out, Bit1);
  not not_8 (not_8_out, Bit0);
  and and_5 (and_5_out, On, Bit1, Bit0);
  and and_6 (and_6_out, On, Bit2);
  and and_7 (and_7_out, On, not_9_out);
  not not_9 (not_9_out, Bit0);
  and and_8 (and_8_out, On, Bit2, not_10_out);
  not not_10 (not_10_out, Bit1);
  and and_9 (and_9_out, On, not_11_out);
  not not_11 (not_11_out, Bit1);
  and and_10 (and_10_out, On, Bit0);
  and and_11 (and_11_out, On, not_12_out);
  not not_12 (not_12_out, Bit2);
  and and_12 (and_12_out, On, not_13_out, not_14_out);
  not not_13 (not_13_out, Bit1);
  not not_14 (not_14_out, Bit0);
  or or_1 (a, and_1_out, and_2_out);
  or or_2 (b, and_3_out, and_4_out);
  and and_13 (and_13_out, On, not_6_out, Bit0);
  or or_3 (c, and_13_out, and_14_out, and_15_out);
  and and_14 (and_14_out, On, not_7_out, Bit0);
  and and_15 (and_15_out, On, Bit2, Bit1, not_8_out);
  or or_4 (d, and_5_out, and_6_out);
  or or_5 (e, and_7_out, and_8_out);
  or or_6 (f, and_9_out, and_10_out);
  or or_7 (g, and_11_out, and_12_out);
endmodule

module \X_Y_Z_espaço  (
  input  On,
  input  Bit2,
  input  Bit1,
  input  Bit0,
  output a,
  output b,
  output c,
  output d,
  output e,
  output f,
  output g
);

  wire and_1_out, and_2_out, and_4_out, and_5_out, and_8_out, and_9_out, not_1_out, not_2_out, not_3_out,
       not_4_out, not_5_out, not_6_out, not_7_out, not_8_out, not_9_out, not_10_out, not_11_out, not_12_out,
       not_13_out, not_14_out, not_15_out, not_16_out, not_17_out, not_18_out, not_19_out, not_20_out;

  not not_1 (not_1_out, Bit2);
  not not_2 (not_2_out, Bit0);
  and and_1 (and_1_out, On, not_3_out, not_4_out);
  not not_3 (not_3_out, Bit2);
  not not_4 (not_4_out, Bit1);
  not not_5 (not_5_out, Bit2);
  and and_2 (and_2_out, On, not_5_out, not_6_out);
  not not_6 (not_6_out, Bit0);
  not not_7 (not_7_out, Bit2);
  not not_8 (not_8_out, Bit1);
  not not_9 (not_9_out, Bit2);
  not not_10 (not_10_out, Bit1);
  not not_11 (not_11_out, Bit2);
  not not_12 (not_12_out, Bit0);
  and and_3 (e, On, not_13_out, not_14_out);
  not not_13 (not_13_out, Bit2);
  not not_14 (not_14_out, Bit0);
  not not_15 (not_15_out, Bit2);
  not not_16 (not_16_out, Bit1);
  not not_17 (not_17_out, Bit2);
  and and_4 (and_4_out, On, not_17_out, not_18_out);
  not not_18 (not_18_out, Bit1);
  and and_5 (and_5_out, On, not_19_out, not_20_out);
  not not_19 (not_19_out, Bit2);
  not not_20 (not_20_out, Bit0);
  and and_6 (a, On, not_1_out, Bit1, not_2_out);
  or or_1 (b, and_1_out, and_2_out);
  and and_7 (c, On, not_7_out, not_8_out, Bit0);
  and and_8 (and_8_out, On, not_9_out, not_10_out, Bit0);
  or or_2 (d, and_8_out, and_9_out);
  and and_9 (and_9_out, On, not_11_out, Bit1, not_12_out);
  and and_10 (f, On, not_15_out, not_16_out, Bit0);
  or or_3 (g, and_4_out, and_5_out);
endmodule
