// Logisim project ZeroTo999Counting.circ as structural Verilog: 2 circuits, main circuit main
module main (
  input  Reverses_the_counting,
  output out_2,
  output out_3,
  output out_4,
  output out_5,
  output out_6,
  output out_7,
  output out_8,
  output out_9,
  output out_10,
  output out_11,
  output out_12,
  output out_13
);

  wire Clock_pulse_out, Hundreds_Digits_Control_a, Hundreds_Digits_Control_b, Hundreds_Digits_Control_c,
       Hundreds_Digits_Control_d, Hundreds_Digits_Control_e, Hundreds_Digits_Control_f,
       Hundreds_Digits_Control_g, Reset_counting_out, Tens_counter_carry, Tens_Digits_Control_a,
       Tens_Digits_Control_b, Tens_Digits_Control_c, Tens_Digits_Control_d, Tens_Digits_Control_e,
       Tens_Digits_Control_f, Tens_Digits_Control_g, Unit_Digits_Control_a, Unit_Digits_Control_b,
       Unit_Digits_Control_c, Unit_Digits_Control_d, Unit_Digits_Control_e, Unit_Digits_Control_f,
       Unit_Digits_Control_g, Units_counter_carry;
  wire [3:0] Hundreds_counter_q, Tens_counter_q, Units_counter_q;

  Button Reset_counting (.out(Reset_counting_out));
  Clock Clock_pulse (.out(Clock_pulse_out));
  Counter #(.width(12), .max('hfff)) Main_counter (
    .load(Reverses_the_counting),
    .Q({out_2, out_3, out_4, out_5, out_6, out_7, out_8, out_9, out_10, out_11, out_12, out_13}),
    .clk(Clock_pulse_out), .clr(Reset_counting_out));  // open: D, count, carry
  Counter #(.width(4), .max('h9), .trigger("falling")) Hundreds_counter (
    .load(Reverses_the_counting), .Q(Hundreds_counter_q), .clk(Tens_counter_carry), .clr(Reset_counting_out));  // open: D, count, carry
  Counter #(.width(4), .max('h9), .trigger("falling")) Tens_counter (
    .load(Reverses_the_counting), .Q(Tens_counter_q), .carry(Tens_counter_carry), .clk(Units_counter_carry),
    .clr(Reset_counting_out));  // open: D, count
  Counter #(.width(4), .max('h9), .trigger("falling")) Units_counter (
    .load(Reverses_the_counting), .Q(Units_counter_q), .carry(Units_counter_carry), .clk(Clock_pulse_out),
    .clr(Reset_counting_out));  // open: D, count
  Digits_Control Hundreds_Digits_Control (
    .Bit3(Hundreds_counter_q[3]), .Bit2(Hundreds_counter_q[2]), .Bit1(Hundreds_counter_q[1]),
    .Bit0(Hundreds_counter_q[0]), .a(Hundreds_Digits_Control_a), .b(Hundreds_Digits_Control_b),
    .c(Hundreds_Digits_Control_c), .d(Hundreds_Digits_Control_d), .e(Hundreds_Digits_Control_e),
    .f(Hundreds_Digits_Control_f), .g(Hundreds_Digits_Control_g));
  Digits_Control Tens_Digits_Control (
    .Bit3(Tens_counter_q[3]), .Bit2(Tens_counter_q[2]), .Bit1(Tens_counter_q[1]), .Bit0(Tens_counter_q[0]),
    .a(Tens_Digits_Control_a), .b(Tens_Digits_Control_b), .c(Tens_Digits_Control_c),
    .d(Tens_Digits_Control_d), .e(Tens_Digits_Control_e), .f(Tens_Digits_Control_f), .g(Tens_Digits_Control_g));
  _7_Segment_Display u_7_segment_display_1 (
    .g(Tens_Digits_Control_g), .f(Tens_Digits_Control_f), .a(Tens_Digits_Control_a),
    .b(Tens_Digits_Control_b), .e(Tens_Digits_Control_e), .d(Tens_Digits_Control_d), .c(Tens_Digits_Control_c));  // open: dp
  _7_Segment_Display u_7_segment_display_2 (
    .g(Hundreds_Digits_Control_g), .f(Hundreds_Digits_Control_f), .a(Hundreds_Digits_Control_a),
    .b(Hundreds_Digits_Control_b), .e(Hundreds_Digits_Control_e), .d(Hundreds_Digits_Control_d),
    .c(Hundreds_Digits_Control_c));  // open: dp
  _7_Segment_Display u_7_segment_display_3 (
    .g(Unit_Digits_Control_g), .f(Unit_Digits_Control_f), .a(Unit_Digits_Control_a),
    .b(Unit_Digits_Control_b), .e(Unit_Digits_Control_e), .d(Unit_Digits_Control_d), .c(Unit_Digits_Control_c));  // open: dp
  Digits_Control Unit_Digits_Control (
    .Bit3(Units_counter_q[3]), .Bit2(Units_counter_q[2]), .Bit1(Units_counter_q[1]),
    .Bit0(Units_counter_q[0]), .a(Unit_Digits_Control_a), .b(Unit_Digits_Control_b),
    .c(Unit_Digits_Control_c), .d(Unit_Digits_Control_d), .e(Unit_Digits_Control_e),
    .f(Unit_Digits_Control_f), .g(Unit_Digits_Control_g));
endmodule

module Digits_Control (
  input  Bit3,
  input  Bit2,
  input  Bit1,
  input  Bit0,
  output a,
  output b,
  output c,
  output d,
  output e,
  output f,
  output g
);

  wire and_1_out, and_2_out, and_3_out, and_4_out, and_5_out, and_6_out, and_7_out, and_8_out, and_9_out,
       and_10_out, and_11_out, and_12_out, and_13_out, and_14_out, and_15_out, and_16_out, and_17_out,
       and_18_out, and_19_out, and_20_out, and_21_out, and_22_out, and_23_out, and_24_out, and_25_out,
       and_26_out, and_27_out, and_28_out, and_29_out, and_30_out, and_31_out, not_1_out, not_2_out,
       not_3_out, not_4_out, not_5_out, not_6_out, not_7_out, not_8_out, not_9_out, not_10_out, not_11_out,
       not_12_out, not_13_out, not_14_out, not_15_out, not_16_out, not_17_out, not_18_out, not_19_out,
       not_20_out, not_21_out, not_22_out, not_23_out, not_24_out, not_25_out, not_26_out, not_27_out,
       not_28_out, not_29_out, not_30_out, not_31_out, not_32_out, not_33_out, not_34_out, not_35_out,
       not_36_out, not_37_out, not_38_out, not_39_out, not_40_out, not_41_out, not_42_out, not_43_out,
       not_44_out;

  not not_1 (not_1_out, Bit2);
  and and_1 (and_1_out, not_1_out, not_2_out);
  not not_2 (not_2_out, Bit0);
  not not_3 (not_3_out, Bit3);
  and and_2 (and_2_out, not_3_out, Bit1);
  and and_3 (and_3_out, Bit2, Bit0);
  and and_4 (and_4_out, Bit3, not_4_out);
  not not_4 (not_4_out, Bit1);
  not not_5 (not_5_out, Bit2);
  not not_6 (not_6_out, Bit1);
  and and_5 (and_5_out, not_6_out, not_7_out);
  not not_7 (not_7_out, Bit0);
  not not_8 (not_8_out, Bit3);
  and and_6 (and_6_out, not_8_out, Bit1, Bit0);
  and and_7 (and_7_out, Bit3, not_9_out);
  not not_9 (not_9_out, Bit1);
  and and_8 (and_8_out, Bit3, not_10_out);
  not not_10 (not_10_out, Bit0);
  not not_11 (not_11_out, Bit3);
  and and_9 (and_9_out, not_11_out, not_12_out);
  not not_12 (not_12_out, Bit1);
  and and_10 (and_10_out, Bit2, Bit1);
  and and_11 (and_11_out, Bit3, not_13_out);
  not not_13 (not_13_out, Bit2);
  not not_14 (not_14_out, Bit2);
  and and_12 (and_12_out, not_14_out, not_15_out);
  not not_15 (not_15_out, Bit0);
  not not_16 (not_16_out, Bit3);
  not not_17 (not_17_out, Bit2);
  and and_13 (and_13_out, not_16_out, not_17_out, Bit1);
  not not_18 (not_18_out, Bit3);
  and and_14 (and_14_out, not_18_out, Bit1, not_19_out);
  not not_19 (not_19_out, Bit0);
  and and_15 (and_15_out, Bit2, not_20_out, Bit0);
  not not_20 (not_20_out, Bit1);
  and and_16 (and_16_out, Bit3, not_21_out, not_22_out);
  not not_21 (not_21_out, Bit1);
  not not_22 (not_22_out, Bit0);
  and and_17 (and_17_out, Bit3, Bit2, Bit0);
  not not_23 (not_23_out, Bit2);
  and and_18 (and_18_out, not_23_out, not_24_out);
  not not_24 (not_24_out, Bit0);
  not not_25 (not_25_out, Bit3);
  and and_19 (and_19_out, not_25_out, Bit1, not_26_out);
  not not_26 (not_26_out, Bit0);
  not not_27 (not_27_out, Bit1);
  and and_20 (and_20_out, Bit3, not_27_out, not_28_out);
  not not_28 (not_28_out, Bit0);
  not not_29 (not_29_out, Bit3);
  not not_30 (not_30_out, Bit1);
  and and_21 (and_21_out, not_29_out, not_30_out, not_31_out);
  not not_31 (not_31_out, Bit0);
  not not_32 (not_32_out, Bit3);
  and and_22 (and_22_out, not_32_out, Bit2, not_33_out);
  not not_33 (not_33_out, Bit1);
  not not_34 (not_34_out, Bit3);
  and and_23 (and_23_out, not_34_out, Bit2, not_35_out);
  not not_35 (not_35_out, Bit0);
  and and_24 (and_24_out, Bit3, not_36_out, not_37_out);
  not not_36 (not_36_out, Bit2);
  not not_37 (not_37_out, Bit1);
  and and_25 (and_25_out, Bit3, not_38_out, not_39_out);
  not not_38 (not_38_out, Bit2);
  not not_39 (not_39_out, Bit0);
  and and_26 (and_26_out, Bit3, Bit2, Bit1);
  not not_40 (not_40_out, Bit3);
  not not_41 (not_41_out, Bit2);
  and and_27 (and_27_out, not_40_out, not_41_out, Bit1);
  and and_28 (and_28_out, Bit2, not_42_out);
  not not_42 (not_42_out, Bit1);
  and and_29 (and_29_out, Bit2, not_43_out);
  not not_43 (not_43_out, Bit0);
  and and_30 (and_30_out, Bit3, not_44_out);
  not not_44 (not_44_out, Bit1);
  and and_31 (and_31_out, Bit3, Bit2);
  or or_1 (a, and_1_out, and_2_out, and_3_out, and_4_out);
  or or_2 (b, not_5_out, and_5_out, and_6_out, and_7_out, and_8_out);
  or or_3 (c, and_9_out, Bit0, and_10_out, and_11_out);
  or or_4 (e, and_18_out, and_19_out, and_20_out);
  or or_5 (g, and_27_out, and_28_out, and_29_out, and_30_out, and_31_out);
  or or_6 (d, and_12_out, and_13_out, and_14_out, and_15_out, and_16_out, and_17_out);
  or or_7 (f, and_21_out, and_22_out, and_23_out, and_24_out, and_25_out, and_26_out);
endmodule
