// Logisim project SilogismosCategoricos.circ as structural Verilog: 31 circuits, main circuit main
module main (
  input  AutoSet_1__ManualSet_0,
  input  EnableManualTick_0,
  input  Count_Revert__1,
  output M_P,
  output P_M,
  output S_M,
  output M_S,
  output out_8,
  output Regra3,
  output out_10,
  output out_11,
  output out_12,
  output out_13,
  output Valid_Argument,
  output [5:0] Valids_binary_counter
);

  wire _1_out, _2_out, _3_out, _4_out, A_2_out, A_3_out, A_out, ctrl_autoclock_or_manualclock_1_carrier,
       ctrl_autoclock_or_manualclock_1_circautomligado_2, ctrl_autoclock_or_manualclock_1_conclusao0_2,
       ctrl_autoclock_or_manualclock_1_conclusao1_2, ctrl_autoclock_or_manualclock_1_fig0_2,
       ctrl_autoclock_or_manualclock_1_fig1_2, ctrl_autoclock_or_manualclock_1_pmaior0_2,
       ctrl_autoclock_or_manualclock_1_pmaior1_2, ctrl_autoclock_or_manualclock_1_pmenor0_2,
       ctrl_autoclock_or_manualclock_1_pmenor1_2, ctrl_autoclock_or_manualclock_1_pulsocontagematual,
       CTRL_SetFigure_a, CTRL_SetFigure_b, CTRL_SetFigure_c, CTRL_SetFigure_d, CTRL_SetFigure_e,
       CTRL_SetFigure_f, CTRL_SetFigure_g, ctrldisplayvalidscounter_1_c1, ctrldisplayvalidscounter_1_c2,
       ctrldisplayvalidscounter_1_c3, ctrldisplayvalidscounter_1_c4, ctrldisplayvalidscounter_1_c5,
       ctrldisplayvalidscounter_1_c6, ctrldisplayvalidscounter_1_c7, ctrldisplayvalidscounter_1_d1,
       ctrldisplayvalidscounter_1_d2, ctrldisplayvalidscounter_1_d3, ctrldisplayvalidscounter_1_d4,
       ctrldisplayvalidscounter_1_d5, ctrldisplayvalidscounter_1_d6, ctrldisplayvalidscounter_1_d7,
       ctrldisplayvalidscounter_1_u1, ctrldisplayvalidscounter_1_u2, ctrldisplayvalidscounter_1_u3,
       ctrldisplayvalidscounter_1_u4, ctrldisplayvalidscounter_1_u5, ctrldisplayvalidscounter_1_u6,
       ctrldisplayvalidscounter_1_u7, ctrldisplayvalidscounter_2_c1, ctrldisplayvalidscounter_2_c2,
       ctrldisplayvalidscounter_2_c3, ctrldisplayvalidscounter_2_c4, ctrldisplayvalidscounter_2_c5,
       ctrldisplayvalidscounter_2_c6, ctrldisplayvalidscounter_2_c7, ctrldisplayvalidscounter_2_d1,
       ctrldisplayvalidscounter_2_d2, ctrldisplayvalidscounter_2_d3, ctrldisplayvalidscounter_2_d4,
       ctrldisplayvalidscounter_2_d5, ctrldisplayvalidscounter_2_d6, ctrldisplayvalidscounter_2_d7,
       ctrldisplayvalidscounter_2_u1, ctrldisplayvalidscounter_2_u2, ctrldisplayvalidscounter_2_u3,
       ctrldisplayvalidscounter_2_u4, ctrldisplayvalidscounter_2_u5, ctrldisplayvalidscounter_2_u6,
       ctrldisplayvalidscounter_2_u7, E_2_out, E_3_out, E_out, exclusive_one_single_selection_ctrl_1_bit0,
       exclusive_one_single_selection_ctrl_1_bit1, exclusive_one_single_selection_ctrl_2_bit0,
       exclusive_one_single_selection_ctrl_2_bit1, exclusive_one_single_selection_ctrl_3_bit0,
       exclusive_one_single_selection_ctrl_3_bit1, exclusive_one_single_selection_ctrl_4_bit0,
       exclusive_one_single_selection_ctrl_4_bit1, I_2_out, I_3_out, I_out, Is_Argument_Valid_valids_counter,
       Manual_Tick_out, O_2_out, O_3_out, O_out, Reset_out, setproposition_1_a, setproposition_1_b,
       setproposition_1_c, setproposition_1_d, setproposition_1_e, setproposition_1_f, setproposition_1_g,
       setproposition_2_a, setproposition_2_b, setproposition_2_c, setproposition_2_d, setproposition_2_e,
       setproposition_2_f, setproposition_2_g, setproposition_3_a, setproposition_3_b, setproposition_3_c,
       setproposition_3_d, setproposition_3_e, setproposition_3_f, setproposition_3_g;

  Button A (.out(A_out));
  Button E (.out(E_out));
  Button I (.out(I_out));
  Button O (.out(O_out));
  SetProposition setproposition_1 (
    .Bit1(exclusive_one_single_selection_ctrl_1_bit1), .Bit0(exclusive_one_single_selection_ctrl_1_bit0),
    .a(setproposition_1_a), .b(setproposition_1_b), .c(setproposition_1_c), .d(setproposition_1_d),
    .e(setproposition_1_e), .f(setproposition_1_f), .g(setproposition_1_g));
  Exclusive_One_Single_Selection_CTRL exclusive_one_single_selection_ctrl_1 (
    .E1(A_out), .E2(E_out), .E3(I_out), .E4(O_out), .Bit1(exclusive_one_single_selection_ctrl_1_bit1),
    .Bit0(exclusive_one_single_selection_ctrl_1_bit0),
    .CircuitoAutomLigado(ctrl_autoclock_or_manualclock_1_circautomligado_2),
    .Bit1_Entrada(ctrl_autoclock_or_manualclock_1_pmaior1_2),
    .Bit0_Entrada(ctrl_autoclock_or_manualclock_1_pmaior0_2));
  bool_Is_Argument_Valid Is_Argument_Valid (
    .regra2(out_8), .regra3(out_10), .regra3b(Regra3), .regra4(out_11), .regra5(out_12), .regra6(out_13),
    .Reset(Reset_out), .SimArgumentoValido(Valid_Argument), .out_9(Valids_binary_counter),
    .Valids_Counter(Is_Argument_Valid_valids_counter));
  _7_Segment_Display u_7_segment_display_1 (
    .g(setproposition_1_g), .f(setproposition_1_f), .a(setproposition_1_a), .b(setproposition_1_b),
    .e(setproposition_1_e), .d(setproposition_1_d), .c(setproposition_1_c));  // open: dp
  Rule_2 Rule_2 (
    .Bit1_Proposicao_PremMaior(ctrl_autoclock_or_manualclock_1_pmaior1_2),
    .Bit0_Proposicao_PremMaior(ctrl_autoclock_or_manualclock_1_pmaior0_2),
    .Bit1_Proposicao_PremMenor(ctrl_autoclock_or_manualclock_1_pmenor1_2),
    .Bit0_Proposicao_PremMenor(ctrl_autoclock_or_manualclock_1_pmenor0_2),
    .Bit1_Figura(ctrl_autoclock_or_manualclock_1_fig1_2),
    .Bit0_Figura(ctrl_autoclock_or_manualclock_1_fig0_2), .ViolaRegra2(out_8));
  Rule_3 Rule_3 (
    .Bit1_PremMaior(ctrl_autoclock_or_manualclock_1_pmaior1_2),
    .Bit0_PremMaior(ctrl_autoclock_or_manualclock_1_pmaior0_2),
    .Bit1_Figura(ctrl_autoclock_or_manualclock_1_fig1_2),
    .Bit0_Figura(ctrl_autoclock_or_manualclock_1_fig0_2),
    .Bit1_PremMenor(ctrl_autoclock_or_manualclock_1_pmenor1_2),
    .Bit0_PremMenor(ctrl_autoclock_or_manualclock_1_pmenor0_2),
    .Bit1_Conclusao(ctrl_autoclock_or_manualclock_1_conclusao1_2),
    .Bit0_Conclusao(ctrl_autoclock_or_manualclock_1_conclusao0_2), .FalaciaProcIlicitoTermoMaior(Regra3),
    .FalaciaProcIlicitoTermoMenor(out_10));
  Rule_4 Rule_4 (
    .Bit1_PremMaior(ctrl_autoclock_or_manualclock_1_pmaior1_2),
    .Bit0_PremMaior(ctrl_autoclock_or_manualclock_1_pmaior0_2),
    .Bit1_PremMenor(ctrl_autoclock_or_manualclock_1_pmenor1_2),
    .Bit0_PremMenor(ctrl_autoclock_or_manualclock_1_pmenor0_2), .FalaciaDasPremissasExclusivas(out_11));
  Rule_5 Rule_5 (
    .Bit1_PremMaior(ctrl_autoclock_or_manualclock_1_pmaior1_2),
    .Bit0_PremMaior(ctrl_autoclock_or_manualclock_1_pmaior0_2),
    .Bit1_PremMenor(ctrl_autoclock_or_manualclock_1_pmenor1_2),
    .Bit0_PremMenor(ctrl_autoclock_or_manualclock_1_pmenor0_2),
    .Bit1_Conclusao(ctrl_autoclock_or_manualclock_1_conclusao1_2),
    .Bit0_Conclusao(ctrl_autoclock_or_manualclock_1_conclusao0_2),
    .FalaciaDaConclusaoAfirmtvaAPartirPremNegativ(out_12));
  Rule_6 Rule_6 (
    .Bit1_PremMaior(ctrl_autoclock_or_manualclock_1_pmaior1_2),
    .Bit0_PremMaior(ctrl_autoclock_or_manualclock_1_pmaior0_2),
    .Bit1_PremMenor(ctrl_autoclock_or_manualclock_1_pmenor1_2),
    .Bit0_PremMenor(ctrl_autoclock_or_manualclock_1_pmenor0_2),
    .Bit1_Conclusao(ctrl_autoclock_or_manualclock_1_conclusao1_2),
    .Bit0_Conclusao(ctrl_autoclock_or_manualclock_1_conclusao0_2), .FalaciaExistencial(out_13));
  Button A_2 (.out(A_2_out));
  Button E_2 (.out(E_2_out));
  Button I_2 (.out(I_2_out));
  Button O_2 (.out(O_2_out));
  SetProposition setproposition_2 (
    .Bit1(exclusive_one_single_selection_ctrl_2_bit1), .Bit0(exclusive_one_single_selection_ctrl_2_bit0),
    .a(setproposition_2_a), .b(setproposition_2_b), .c(setproposition_2_c), .d(setproposition_2_d),
    .e(setproposition_2_e), .f(setproposition_2_f), .g(setproposition_2_g));
  Exclusive_One_Single_Selection_CTRL exclusive_one_single_selection_ctrl_2 (
    .E1(A_2_out), .E2(E_2_out), .E3(I_2_out), .E4(O_2_out),
    .Bit1(exclusive_one_single_selection_ctrl_2_bit1), .Bit0(exclusive_one_single_selection_ctrl_2_bit0),
    .CircuitoAutomLigado(ctrl_autoclock_or_manualclock_1_circautomligado_2),
    .Bit1_Entrada(ctrl_autoclock_or_manualclock_1_pmenor1_2),
    .Bit0_Entrada(ctrl_autoclock_or_manualclock_1_pmenor0_2));
  _7_Segment_Display u_7_segment_display_2 (
    .g(setproposition_2_g), .f(setproposition_2_f), .a(setproposition_2_a), .b(setproposition_2_b),
    .e(setproposition_2_e), .d(setproposition_2_d), .c(setproposition_2_c));  // open: dp
  CTRL_AutoClock_Or_ManualClock ctrl_autoclock_or_manualclock_1 (
    .CircAutomLigado(AutoSet_1__ManualSet_0), .Reverse(Count_Revert__1), .Reset(Reset_out),
    .Tick_Manual(Manual_Tick_out), .CircAutomLigado_2(ctrl_autoclock_or_manualclock_1_circautomligado_2),
    .Fig0_2(ctrl_autoclock_or_manualclock_1_fig0_2), .Fig1_2(ctrl_autoclock_or_manualclock_1_fig1_2),
    .PMaior0_2(ctrl_autoclock_or_manualclock_1_pmaior0_2), .Carrier(ctrl_autoclock_or_manualclock_1_carrier),
    .PMaior1_2(ctrl_autoclock_or_manualclock_1_pmaior1_2),
    .PMenor0_2(ctrl_autoclock_or_manualclock_1_pmenor0_2),
    .PMenor1_2(ctrl_autoclock_or_manualclock_1_pmenor1_2),
    .Conclusao0_2(ctrl_autoclock_or_manualclock_1_conclusao0_2),
    .Conclusao1_2(ctrl_autoclock_or_manualclock_1_conclusao1_2),
    .PulsoContagemAtual(ctrl_autoclock_or_manualclock_1_pulsocontagematual),
    .Fig0(exclusive_one_single_selection_ctrl_4_bit0), .Fig1(exclusive_one_single_selection_ctrl_4_bit1),
    .PMaior0(exclusive_one_single_selection_ctrl_1_bit0),
    .PMaior1(exclusive_one_single_selection_ctrl_1_bit1),
    .PMenor0(exclusive_one_single_selection_ctrl_2_bit0),
    .PMenor1(exclusive_one_single_selection_ctrl_2_bit1),
    .Conclusao0(exclusive_one_single_selection_ctrl_3_bit0),
    .Conclusao1(exclusive_one_single_selection_ctrl_3_bit1), .ClockManual_0(EnableManualTick_0));
  Button Manual_Tick (.out(Manual_Tick_out));
  Button A_3 (.out(A_3_out));
  Button E_3 (.out(E_3_out));
  Button I_3 (.out(I_3_out));
  Button O_3 (.out(O_3_out));
  Button Reset (.out(Reset_out));
  SetProposition setproposition_3 (
    .Bit1(exclusive_one_single_selection_ctrl_3_bit1), .Bit0(exclusive_one_single_selection_ctrl_3_bit0),
    .a(setproposition_3_a), .b(setproposition_3_b), .c(setproposition_3_c), .d(setproposition_3_d),
    .e(setproposition_3_e), .f(setproposition_3_f), .g(setproposition_3_g));
  Exclusive_One_Single_Selection_CTRL exclusive_one_single_selection_ctrl_3 (
    .E1(A_3_out), .E2(E_3_out), .E3(I_3_out), .E4(O_3_out),
    .Bit1(exclusive_one_single_selection_ctrl_3_bit1), .Bit0(exclusive_one_single_selection_ctrl_3_bit0),
    .CircuitoAutomLigado(ctrl_autoclock_or_manualclock_1_circautomligado_2),
    .Bit1_Entrada(ctrl_autoclock_or_manualclock_1_conclusao1_2),
    .Bit0_Entrada(ctrl_autoclock_or_manualclock_1_conclusao0_2));
  _7_Segment_Display u_7_segment_display_3 (
    .g(setproposition_3_g), .f(setproposition_3_f), .a(setproposition_3_a), .b(setproposition_3_b),
    .e(setproposition_3_e), .d(setproposition_3_d), .c(setproposition_3_c));  // open: dp
  Button _1 (.out(_1_out));
  Button _2 (.out(_2_out));
  Button _3 (.out(_3_out));
  Button _4 (.out(_4_out));
  CTRLDisplayValidsCounter ctrldisplayvalidscounter_1 (
    .ReiniciaContagem(Reset_out), .Contador(ctrl_autoclock_or_manualclock_1_pulsocontagematual),
    .RevertCount(Count_Revert__1), .u1(ctrldisplayvalidscounter_1_u1), .u2(ctrldisplayvalidscounter_1_u2),
    .u3(ctrldisplayvalidscounter_1_u3), .u4(ctrldisplayvalidscounter_1_u4),
    .u5(ctrldisplayvalidscounter_1_u5), .u6(ctrldisplayvalidscounter_1_u6),
    .u7(ctrldisplayvalidscounter_1_u7), .d1(ctrldisplayvalidscounter_1_d1),
    .d2(ctrldisplayvalidscounter_1_d2), .d3(ctrldisplayvalidscounter_1_d3),
    .d4(ctrldisplayvalidscounter_1_d4), .d5(ctrldisplayvalidscounter_1_d5),
    .d6(ctrldisplayvalidscounter_1_d6), .d7(ctrldisplayvalidscounter_1_d7),
    .c1(ctrldisplayvalidscounter_1_c1), .c2(ctrldisplayvalidscounter_1_c2),
    .c3(ctrldisplayvalidscounter_1_c3), .c4(ctrldisplayvalidscounter_1_c4),
    .c5(ctrldisplayvalidscounter_1_c5), .c6(ctrldisplayvalidscounter_1_c6), .c7(ctrldisplayvalidscounter_1_c7));
  _7_Segment_Display u_7_segment_display_4 (
    .g(CTRL_SetFigure_g), .f(CTRL_SetFigure_f), .a(CTRL_SetFigure_a), .b(CTRL_SetFigure_b),
    .e(CTRL_SetFigure_e), .d(CTRL_SetFigure_d), .c(CTRL_SetFigure_c));  // open: dp
  Exclusive_One_Single_Selection_CTRL exclusive_one_single_selection_ctrl_4 (
    .E1(_1_out), .E2(_2_out), .E3(_3_out), .E4(_4_out), .Bit1(exclusive_one_single_selection_ctrl_4_bit1),
    .Bit0(exclusive_one_single_selection_ctrl_4_bit0),
    .CircuitoAutomLigado(ctrl_autoclock_or_manualclock_1_circautomligado_2),
    .Bit1_Entrada(ctrl_autoclock_or_manualclock_1_fig1_2),
    .Bit0_Entrada(ctrl_autoclock_or_manualclock_1_fig0_2));
  _7_Segment_Display u_7_segment_display_5 (
    .g(ctrldisplayvalidscounter_1_c7), .f(ctrldisplayvalidscounter_1_c6), .a(ctrldisplayvalidscounter_1_c1),
    .b(ctrldisplayvalidscounter_1_c2), .e(ctrldisplayvalidscounter_1_c5), .d(ctrldisplayvalidscounter_1_c4),
    .c(ctrldisplayvalidscounter_1_c3));  // open: dp
  CTRLDisplayValidsCounter ctrldisplayvalidscounter_2 (
    .ReiniciaContagem(ctrl_autoclock_or_manualclock_1_carrier), .Contador(Is_Argument_Valid_valids_counter),
    .RevertCount(Count_Revert__1), .u1(ctrldisplayvalidscounter_2_u1), .u2(ctrldisplayvalidscounter_2_u2),
    .u3(ctrldisplayvalidscounter_2_u3), .u4(ctrldisplayvalidscounter_2_u4),
    .u5(ctrldisplayvalidscounter_2_u5), .u6(ctrldisplayvalidscounter_2_u6),
    .u7(ctrldisplayvalidscounter_2_u7), .d1(ctrldisplayvalidscounter_2_d1),
    .d2(ctrldisplayvalidscounter_2_d2), .d3(ctrldisplayvalidscounter_2_d3),
    .d4(ctrldisplayvalidscounter_2_d4), .d5(ctrldisplayvalidscounter_2_d5),
    .d6(ctrldisplayvalidscounter_2_d6), .d7(ctrldisplayvalidscounter_2_d7),
    .c1(ctrldisplayvalidscounter_2_c1), .c2(ctrldisplayvalidscounter_2_c2),
    .c3(ctrldisplayvalidscounter_2_c3), .c4(ctrldisplayvalidscounter_2_c4),
    .c5(ctrldisplayvalidscounter_2_c5), .c6(ctrldisplayvalidscounter_2_c6), .c7(ctrldisplayvalidscounter_2_c7));
  _7_Segment_Display u_7_segment_display_6 (
    .g(ctrldisplayvalidscounter_1_d7), .f(ctrldisplayvalidscounter_1_d6), .a(ctrldisplayvalidscounter_1_d1),
    .b(ctrldisplayvalidscounter_1_d2), .e(ctrldisplayvalidscounter_1_d5), .d(ctrldisplayvalidscounter_1_d4),
    .c(ctrldisplayvalidscounter_1_d3));  // open: dp
  _7_Segment_Display u_7_segment_display_7 (
    .g(ctrldisplayvalidscounter_1_u7), .f(ctrldisplayvalidscounter_1_u6), .a(ctrldisplayvalidscounter_1_u1),
    .b(ctrldisplayvalidscounter_1_u2), .e(ctrldisplayvalidscounter_1_u5), .d(ctrldisplayvalidscounter_1_u4),
    .c(ctrldisplayvalidscounter_1_u3));  // open: dp
  CTRL_SetFigure CTRL_SetFigure (
    .Bit1_PremMenor(exclusive_one_single_selection_ctrl_4_bit1),
    .Bit0_PremMaior(exclusive_one_single_selection_ctrl_4_bit0), .a(CTRL_SetFigure_a), .b(CTRL_SetFigure_b),
    .c(CTRL_SetFigure_c), .d(CTRL_SetFigure_d), .e(CTRL_SetFigure_e), .f(CTRL_SetFigure_f),
    .g(CTRL_SetFigure_g));
  _7_Segment_Display u_7_segment_display_8 (
    .g(ctrldisplayvalidscounter_2_d7), .f(ctrldisplayvalidscounter_2_d6), .a(ctrldisplayvalidscounter_2_d1),
    .b(ctrldisplayvalidscounter_2_d2), .e(ctrldisplayvalidscounter_2_d5), .d(ctrldisplayvalidscounter_2_d4),
    .c(ctrldisplayvalidscounter_2_d3));  // open: dp
  _7_Segment_Display u_7_segment_display_9 (
    .g(ctrldisplayvalidscounter_2_c7), .f(ctrldisplayvalidscounter_2_c6), .a(ctrldisplayvalidscounter_2_c1),
    .b(ctrldisplayvalidscounter_2_c2), .e(ctrldisplayvalidscounter_2_c5), .d(ctrldisplayvalidscounter_2_c4),
    .c(ctrldisplayvalidscounter_2_c3));  // open: dp
  Terms Termos (
    .Bit1(exclusive_one_single_selection_ctrl_4_bit1), .Bit0(exclusive_one_single_selection_ctrl_4_bit0),
    .M_P(M_P), .P_M(P_M), .S_M(S_M), .M_S(M_S));
  _7_Segment_Display u_7_segment_display_10 (
    .g(ctrldisplayvalidscounter_2_u7), .f(ctrldisplayvalidscounter_2_u6), .a(ctrldisplayvalidscounter_2_u1),
    .b(ctrldisplayvalidscounter_2_u2), .e(ctrldisplayvalidscounter_2_u5), .d(ctrldisplayvalidscounter_2_u4),
    .c(ctrldisplayvalidscounter_2_u3));  // open: dp

  // Notes on the sheet:
  //   Valids_binary_counter: pull=up
  //   Regra2
  //   Falácia do termo médio não distribuído
  //   Falácia Ilícito Maior
  //   Falácia Ilícito Menor
  //   Regra4
  //   Falácia das premissas exclusivas
  //   Regra5
  //   Falc concl. positv sobre prem. ngtv
  //   Regra6
  //   Falacia existencial
  //   Argumento Válido?
  //   Premissa maior
  //   Premissa menor
  //   Fonte doutrinária: Introdução à Lógica - Irving Copi (Cap. 6)
  //   Doctrinal source: Introduction to Logic - Irving Copi (Chap. 6)
  //   Silogismos categóricos de forma típica
  //   Conclusão
  //   Figura
  //   Nr Argumento Atual
  //   Conta args válidos
  //   S-P
  //   S-P
endmodule

module CTRL_AutoClock_Or_ManualClock (
  input  CircAutomLigado,
  input  Fig0,
  input  Reverse,
  input  Fig1,
  input  Reset,
  input  ClockManual_0,
  input  PMaior0,
  input  Tick_Manual,
  input  PMaior1,
  input  PMenor0,
  input  PMenor1,
  input  Conclusao0,
  input  Conclusao1,
  output CircAutomLigado_2,
  output Fig0_2,
  output Fig1_2,
  output PMaior0_2,
  output PMaior1_2,
  output Carrier,
  output PMenor0_2,
  output PulsoContagemAtual,
  output PMenor1_2,
  output Conclusao0_2,
  output Conclusao1_2
);

  wire and_1_out, and_2_out, and_3_out, and_4_out, and_5_out, and_6_out, and_7_out, and_8_out, and_9_out,
       and_10_out, and_11_out, and_12_out, and_13_out, and_14_out, and_15_out, and_16_out, and_17_out,
       clock_1_out, counter_1_carry, not_1_out;
  wire [7:0] counter_1_q;

  and and_1 (and_1_out, ClockManual_0, clock_1_out);
  Clock clock_1 (.out(clock_1_out));
  Counter #(.trigger("falling")) counter_1 (
    .load(Reverse), .Q(counter_1_q), .carry(counter_1_carry), .clk(PulsoContagemAtual), .clr(Reset));  // open: D, count
  or or_1 (PulsoContagemAtual, and_1_out, Tick_Manual);
  or or_2 (Carrier, Reset, counter_1_carry);
  not not_1 (not_1_out, CircAutomLigado);
  and and_2 (and_2_out, Fig0, not_1_out);
  or or_3 (Fig0_2, and_2_out, and_3_out);
  and and_3 (and_3_out, counter_1_q[0], CircAutomLigado);
  and and_4 (and_4_out, Fig1, not_1_out);
  or or_4 (Fig1_2, and_4_out, and_5_out);
  and and_5 (and_5_out, counter_1_q[1], CircAutomLigado);
  and and_6 (and_6_out, PMaior0, not_1_out);
  and and_7 (and_7_out, counter_1_q[2], CircAutomLigado);
  and and_8 (and_8_out, PMaior1, not_1_out);
  and and_9 (and_9_out, counter_1_q[3], CircAutomLigado);
  and and_10 (and_10_out, PMenor0, not_1_out);
  and and_11 (and_11_out, counter_1_q[4], CircAutomLigado);
  and and_12 (and_12_out, PMenor1, not_1_out);
  and and_13 (and_13_out, counter_1_q[5], CircAutomLigado);
  and and_14 (and_14_out, Conclusao0, not_1_out);
  and and_15 (and_15_out, counter_1_q[6], CircAutomLigado);
  and and_16 (and_16_out, Conclusao1, not_1_out);
  and and_17 (and_17_out, counter_1_q[7], CircAutomLigado);
  or or_5 (PMaior0_2, and_6_out, and_7_out);
  or or_6 (PMaior1_2, and_8_out, and_9_out);
  or or_7 (PMenor0_2, and_10_out, and_11_out);
  or or_8 (PMenor1_2, and_12_out, and_13_out);
  or or_9 (Conclusao0_2, and_14_out, and_15_out);
  or or_10 (Conclusao1_2, and_16_out, and_17_out);

  assign CircAutomLigado_2 = CircAutomLigado;
endmodule

module Exclusive_One_Single_Selection_CTRL (
  input  Bit0_Entrada,
  input  Bit1_Entrada,
  input  E1,
  input  E2,
  input  E3,
  input  E4,
  input  CircuitoAutomLigado,
  output Bit1,
  output Bit0
);

  wire and_1_out, and_2_out, and_3_out, and_4_out, button_1_out, button_2_out, button_3_out, button_4_out,
       button_5_out, button_6_out, button_7_out, button_8_out, button_9_out, button_10_out, button_11_out,
       clock_1_out, d_ff_1_q, d_ff_2_q, d_ff_3_q, d_ff_4_q, input2output4_1_s1, input2output4_1_s2,
       input2output4_1_s3, input2output4_1_s4, or_1_out, or_2_out, or_3_out, or_4_out, or_5_out, or_6_out,
       or_7_out, or_8_out, or_9_out, or_10_out, or_11_out, or_12_out, or_13_out, or_14_out, or_15_out;

  Button button_1 (.out(button_1_out));
  or or_1 (or_1_out, button_1_out, CircuitoAutomLigado);
  or or_2 (or_2_out, Bit0_Entrada, button_6_out);
  Input2Output4 input2output4_1 (
    .Bit1(or_3_out), .Bit0(or_2_out), .S1(input2output4_1_s1), .S2(input2output4_1_s2),
    .S3(input2output4_1_s3), .S4(input2output4_1_s4));
  or or_3 (or_3_out, button_7_out, Bit1_Entrada);
  and and_1 (and_1_out, input2output4_1_s1, or_1_out);
  Button button_2 (.out(button_2_out));
  and and_2 (and_2_out, input2output4_1_s2, or_1_out);
  Button button_3 (.out(button_3_out));
  and and_3 (and_3_out, input2output4_1_s3, or_1_out);
  Button button_4 (.out(button_4_out));
  and and_4 (and_4_out, input2output4_1_s4, or_1_out);
  Button button_5 (.out(button_5_out));
  Button button_6 (.out(button_6_out));
  or or_4 (or_4_out, and_1_out, button_2_out, E1);
  or or_5 (or_5_out, and_2_out, button_3_out, E2);
  or or_6 (or_6_out, and_3_out, button_4_out, E3);
  Clock clock_1 (.out(clock_1_out));
  or or_7 (or_7_out, and_4_out, button_5_out, E4);
  Button button_7 (.out(button_7_out));
  D_Flip_Flop d_ff_1 (.clk(clock_1_out), .Q(d_ff_1_q), .preset(or_4_out), .reset(or_8_out));  // open: D, Qn, en
  Button button_8 (.out(button_8_out));
  or or_8 (or_8_out, button_8_out, or_9_out);
  or or_9 (or_9_out, or_7_out, or_6_out, or_5_out);
  D_Flip_Flop d_ff_2 (.clk(clock_1_out), .Q(d_ff_2_q), .preset(or_5_out), .reset(or_10_out));  // open: D, Qn, en
  Button button_9 (.out(button_9_out));
  or or_10 (or_10_out, button_9_out, or_11_out);
  or or_11 (or_11_out, or_4_out, or_7_out, or_6_out);
  D_Flip_Flop d_ff_3 (.clk(clock_1_out), .Q(d_ff_3_q), .preset(or_6_out), .reset(or_12_out));  // open: D, Qn, en
  Button button_10 (.out(button_10_out));
  or or_12 (or_12_out, button_10_out, or_13_out);
  or or_13 (or_13_out, or_4_out, or_5_out, or_7_out);
  D_Flip_Flop d_ff_4 (.clk(clock_1_out), .Q(d_ff_4_q), .preset(or_7_out), .reset(or_14_out));  // open: D, Qn, en
  Button button_11 (.out(button_11_out));
  or or_14 (or_14_out, button_11_out, or_15_out);
  or or_15 (or_15_out, or_4_out, or_5_out, or_6_out);
  Input4Output2 input4output2_1 (.A(d_ff_1_q), .E(d_ff_2_q), .I(d_ff_3_q), .O(d_ff_4_q), .bit1(Bit1), .bit0(Bit0));
endmodule

module bool_Is_DistributdSubject (
  input  bit1,
  input  bit0,
  output simDistribuiSujeito
);

  not not_1 (simDistribuiSujeito, bit1);
endmodule

module bool_Is_DistributdPredicate (
  input  Bit1,
  input  Bit0,
  output SimDistribuiPredicado
);


  assign SimDistribuiPredicado = Bit0;
endmodule

module bool_Does_FigureInverts_MP (
  input  Bit1,
  input  Bit0,
  output SimInverteMP
);


  assign SimInverteMP = Bit0;
endmodule

module bool_Does_FigureInverts_SM (
  input  Bit1,
  input  Bit0,
  output SimInverteSM
);


  assign SimInverteSM = Bit1;
endmodule

module bool_Is_MediumTermDistbted (
  input  Bit1_Proposicao_PremMaior,
  input  Bit0_Proposicao_PremMaior,
  input  Bit1_Proposicao_PremMenor,
  input  Bit0_Proposicao_PremMenor,
  input  Bit1_Figura,
  input  Bit0_Figura,
  output SimlTermoMedioDistrbuido
);

  wire boolTermMedDistNaPremMaior_simtmdistrnapremmaior, boolTermMedDistNaPremMenor_simtmdistrnapremmenor;

  bool_Is_MediumTermDistbOnMajorPremiss boolTermMedDistNaPremMaior (
    .Bit1_Proposicao(Bit1_Proposicao_PremMaior), .Bit0_Proposicao(Bit0_Proposicao_PremMaior),
    .Bit1_Figura(Bit1_Figura), .Bit0_Figura(Bit0_Figura),
    .SimTMDistrNaPremMaior(boolTermMedDistNaPremMaior_simtmdistrnapremmaior));
  bool_Is_MediumTermDistbOnMinorPremiss boolTermMedDistNaPremMenor (
    .Bit1_Proposicao(Bit1_Proposicao_PremMenor), .Bit0_Proposicao(Bit0_Proposicao_PremMenor),
    .Bit1_Figura(Bit1_Figura), .Bit0_Figura(Bit0_Figura),
    .SimTMDistrNaPremMenor(boolTermMedDistNaPremMenor_simtmdistrnapremmenor));
  or or_1 (SimlTermoMedioDistrbuido, boolTermMedDistNaPremMaior_simtmdistrnapremmaior, boolTermMedDistNaPremMenor_simtmdistrnapremmenor);
endmodule

module bool_Is_MediumTermDistbOnMajorPremiss (
  input  Bit1_Proposicao,
  input  Bit0_Proposicao,
  input  Bit1_Figura,
  input  Bit0_Figura,
  output SimTMDistrNaPremMaior
);

  wire and_1_out, and_2_out, boolDistribuiPredicado_simdistribuipredicado,
       boolDistribuiSujeito_simdistribuisujeito, boolFiguraInverteMP_siminvertemp, not_1_out;

  bool_Does_FigureInverts_MP boolFiguraInverteMP (
    .Bit1(Bit1_Figura), .Bit0(Bit0_Figura), .SimInverteMP(boolFiguraInverteMP_siminvertemp));
  bool_Is_DistributdSubject boolDistribuiSujeito (
    .bit1(Bit1_Proposicao), .bit0(Bit0_Proposicao),
    .simDistribuiSujeito(boolDistribuiSujeito_simdistribuisujeito));
  bool_Is_DistributdPredicate boolDistribuiPredicado (
    .Bit1(Bit1_Proposicao), .Bit0(Bit0_Proposicao),
    .SimDistribuiPredicado(boolDistribuiPredicado_simdistribuipredicado));
  not not_1 (not_1_out, boolFiguraInverteMP_siminvertemp);
  and and_1 (and_1_out, boolDistribuiSujeito_simdistribuisujeito, not_1_out);
  and and_2 (and_2_out, boolDistribuiPredicado_simdistribuipredicado, boolFiguraInverteMP_siminvertemp);
  or or_1 (SimTMDistrNaPremMaior, and_1_out, and_2_out);
endmodule

module bool_Is_MediumTermDistbOnMinorPremiss (
  input  Bit1_Proposicao,
  input  Bit0_Proposicao,
  input  Bit1_Figura,
  input  Bit0_Figura,
  output SimTMDistrNaPremMenor
);

  wire and_1_out, and_2_out, boolDistribuiPredicado_simdistribuipredicado,
       boolDistribuiSujeito_simdistribuisujeito, boolFiguraInverteSM_siminvertesm, not_1_out;

  bool_Does_FigureInverts_SM boolFiguraInverteSM (
    .Bit1(Bit1_Figura), .Bit0(Bit0_Figura), .SimInverteSM(boolFiguraInverteSM_siminvertesm));
  bool_Is_DistributdSubject boolDistribuiSujeito (
    .bit1(Bit1_Proposicao), .bit0(Bit0_Proposicao),
    .simDistribuiSujeito(boolDistribuiSujeito_simdistribuisujeito));
  bool_Is_DistributdPredicate boolDistribuiPredicado (
    .Bit1(Bit1_Proposicao), .Bit0(Bit0_Proposicao),
    .SimDistribuiPredicado(boolDistribuiPredicado_simdistribuipredicado));
  not not_1 (not_1_out, boolFiguraInverteSM_siminvertesm);
  and and_1 (and_1_out, boolDistribuiPredicado_simdistribuipredicado, not_1_out);
  and and_2 (and_2_out, boolDistribuiSujeito_simdistribuisujeito, boolFiguraInverteSM_siminvertesm);
  or or_1 (SimTMDistrNaPremMenor, and_1_out, and_2_out);
endmodule

module bool_Is_SubjtDistribOnMinorPremiss (
  input  Bit1_Proposicao_PremMenor,
  input  Bit0_Proposicao_PremMenor,
  input  Bit1_Figura,
  input  Bit0_Figura,
  output SimSujeitoDistrbuidoNaPMenor
);

  wire and_1_out, and_2_out, boolDistribuiPredicado_simdistribuipredicado,
       boolDistribuiSujeito_simdistribuisujeito, boolFiguraInverteSM_siminvertesm, not_1_out;

  bool_Does_FigureInverts_SM boolFiguraInverteSM (
    .Bit1(Bit1_Figura), .Bit0(Bit0_Figura), .SimInverteSM(boolFiguraInverteSM_siminvertesm));
  bool_Is_DistributdPredicate boolDistribuiPredicado (
    .Bit1(Bit1_Proposicao_PremMenor), .Bit0(Bit0_Proposicao_PremMenor),
    .SimDistribuiPredicado(boolDistribuiPredicado_simdistribuipredicado));
  bool_Is_DistributdSubject boolDistribuiSujeito (
    .bit1(Bit1_Proposicao_PremMenor), .bit0(Bit0_Proposicao_PremMenor),
    .simDistribuiSujeito(boolDistribuiSujeito_simdistribuisujeito));
  not not_1 (not_1_out, boolFiguraInverteSM_siminvertesm);
  and and_1 (and_1_out, boolDistribuiPredicado_simdistribuipredicado, boolFiguraInverteSM_siminvertesm);
  and and_2 (and_2_out, boolDistribuiSujeito_simdistribuisujeito, not_1_out);
  or or_1 (SimSujeitoDistrbuidoNaPMenor, and_1_out, and_2_out);
endmodule

module bool_Is_DistrbPredicOnMajorPremiss (
  input  Bit1_Proposicao_PremMaior,
  input  Bit0_Proposicao_PremMaior,
  input  Bit1_Figura,
  input  Bit0_Figura,
  output SimPredicdoDistrbuidoNaPMaior
);

  wire and_1_out, and_2_out, boolDistribuiPredicado_simdistribuipredicado,
       boolDistribuiSujeito_simdistribuisujeito, boolFiguraInverteMP_siminvertemp, not_1_out;

  bool_Does_FigureInverts_MP boolFiguraInverteMP (
    .Bit1(Bit1_Figura), .Bit0(Bit0_Figura), .SimInverteMP(boolFiguraInverteMP_siminvertemp));
  bool_Is_DistributdPredicate boolDistribuiPredicado (
    .Bit1(Bit1_Proposicao_PremMaior), .Bit0(Bit0_Proposicao_PremMaior),
    .SimDistribuiPredicado(boolDistribuiPredicado_simdistribuipredicado));
  bool_Is_DistributdSubject boolDistribuiSujeito (
    .bit1(Bit1_Proposicao_PremMaior), .bit0(Bit0_Proposicao_PremMaior),
    .simDistribuiSujeito(boolDistribuiSujeito_simdistribuisujeito));
  not not_1 (not_1_out, boolFiguraInverteMP_siminvertemp);
  and and_1 (and_1_out, boolDistribuiSujeito_simdistribuisujeito, boolFiguraInverteMP_siminvertemp);
  and and_2 (and_2_out, boolDistribuiPredicado_simdistribuipredicado, not_1_out);
  or or_1 (SimPredicdoDistrbuidoNaPMaior, and_1_out, and_2_out);
endmodule

module bool_Is_MajorPremNegative (
  input  Bit1_PremMaior,
  input  Bit0_PremMaior,
  output SimPremMaiorNegativa
);


  assign SimPremMaiorNegativa = Bit0_PremMaior;
endmodule

module bool_Is_MinorPremNegative (
  input  Bit1_PremMenor,
  input  Bit0_PremMenor,
  output SimPremMenorNegativa
);


  assign SimPremMenorNegativa = Bit0_PremMenor;
endmodule

module boolAfirmatvConclusion (
  input  Bit1_Conclusao,
  input  Bit0_Conclusao,
  output SimConclusaoAfirmativa
);

  not not_1 (SimConclusaoAfirmativa, Bit0_Conclusao);
endmodule

module bool_Universal_Major_Premiss (
  input  Bit1_PremMaior,
  input  Bit0_PremMaior,
  output SimPremMaiorUniversal
);

  not not_1 (SimPremMaiorUniversal, Bit1_PremMaior);
endmodule

module bool_Universal_Minor_Premiss (
  input  Bit1_PremMenor,
  input  Bit0_PremMenor,
  output SimPremMenorUniversal
);

  not not_1 (SimPremMenorUniversal, Bit1_PremMenor);
endmodule

module bool_IsEspecificConclusion (
  input  Bit1_Conclusao,
  input  Bit0_Conclusao,
  output SimConclusaoParticular
);


  assign SimConclusaoParticular = Bit1_Conclusao;
endmodule

module Input4Output2 (
  input  A,
  input  E,
  input  I,
  input  O,
  output bit1,
  output bit0
);

  wire and_1_out, and_2_out, not_1_out, not_2_out, not_3_out, not_4_out;

  not not_1 (not_1_out, A);
  and and_1 (and_1_out, not_1_out, not_2_out);
  not not_2 (not_2_out, E);
  not not_3 (not_3_out, A);
  and and_2 (and_2_out, not_3_out, not_4_out);
  not not_4 (not_4_out, I);
  or or_1 (bit1, and_1_out, O, I);
  or or_2 (bit0, and_2_out, O, E);
endmodule

module CTRL_SetFigure (
  input  Bit1_PremMenor,
  input  Bit0_PremMaior,
  output a,
  output b,
  output c,
  output d,
  output e,
  output f,
  output g
);

  wire and_2_out, and_3_out, and_4_out, and_5_out, not_1_out, not_2_out, not_3_out, not_4_out, not_5_out,
       not_6_out;

  not not_1 (not_1_out, Bit1_PremMenor);
  not not_2 (not_2_out, Bit0_PremMaior);
  not not_3 (not_3_out, Bit0_PremMaior);
  not not_4 (not_4_out, Bit1_PremMenor);
  not not_5 (not_5_out, Bit0_PremMaior);
  not not_6 (not_6_out, Bit1_PremMenor);
  and and_1 (f, Bit1_PremMenor, Bit0_PremMaior);
  or or_1 (g, Bit0_PremMaior, Bit1_PremMenor);
  and and_2 (and_2_out, not_1_out, Bit0_PremMaior);
  or or_2 (a, and_2_out, and_3_out);
  and and_3 (and_3_out, Bit1_PremMenor, not_2_out);
  or or_3 (c, not_3_out, Bit1_PremMenor);
  and and_4 (and_4_out, not_4_out, Bit0_PremMaior);
  or or_4 (d, and_4_out, and_5_out);
  and and_5 (and_5_out, Bit1_PremMenor, not_5_out);
  and and_6 (e, not_6_out, Bit0_PremMaior);

  assign b = 1'b1;
endmodule

module SetProposition (
  input  Bit1,
  input  Bit0,
  output a,
  output b,
  output c,
  output d,
  output e,
  output f,
  output g
);

  wire not_1_out, not_2_out, not_3_out, not_4_out, not_5_out;

  not not_1 (not_1_out, Bit1);
  not not_2 (not_2_out, Bit0);
  not not_3 (not_3_out, Bit0);
  not not_4 (not_4_out, Bit1);
  not not_5 (not_5_out, Bit1);
  not not_6 (g, Bit1);
  or or_1 (a, not_1_out, Bit0);
  or or_2 (b, not_2_out, Bit1);
  or or_3 (c, not_3_out, Bit1);
  or or_4 (e, not_4_out, Bit0);
  or or_5 (f, not_5_out, Bit0);

  assign d = Bit0;
endmodule

module Terms (
  input  Bit1,
  input  Bit0,
  output M_P,
  output P_M,
  output S_M,
  output M_S
);

  not not_1 (M_P, Bit0);
  not not_2 (S_M, Bit1);

  assign M_S = Bit1;
  assign P_M = Bit0;
endmodule

module Input2Output4 (
  input  Bit1,
  input  Bit0,
  output S1,
  output S2,
  output S3,
  output S4
);

  wire button_1_out, button_2_out, not_1_out, not_2_out, not_3_out, not_4_out, or_1_out, or_2_out;

  or or_1 (or_1_out, Bit1, button_1_out);
  Button button_1 (.out(button_1_out));
  or or_2 (or_2_out, Bit0, button_2_out);
  Button button_2 (.out(button_2_out));
  not not_1 (not_1_out, or_1_out);
  not not_2 (not_2_out, or_2_out);
  not not_3 (not_3_out, or_1_out);
  not not_4 (not_4_out, or_2_out);
  and and_1 (S1, not_1_out, not_2_out);
  and and_2 (S2, not_3_out, or_2_out);
  and and_3 (S3, or_1_out, not_4_out);
  and and_4 (S4, or_1_out, or_2_out);
endmodule

module CTRLDisplayValidsCounter (
  input  ReiniciaContagem,
  input  Contador,
  input  RevertCount,
  output u1,
  output u2,
  output u3,
  output u4,
  output u5,
  output u6,
  output u7,
  output d1,
  output d2,
  output d3,
  output d4,
  output d5,
  output d6,
  output d7,
  output c1,
  output c2,
  output c3,
  output c4,
  output c5,
  output c6,
  output c7
);

  wire button_1_out, button_2_out, button_3_out, counter_1_carry, counter_3_carry, counter_4_carry, or_1_out,
       or_2_out, or_3_out, or_4_out;
  wire [3:0] counter_2_q, counter_3_q, counter_4_q;

  Button button_1 (.out(button_1_out));
  or or_1 (or_1_out, button_1_out, ReiniciaContagem);
  Button button_2 (.out(button_2_out));
  or or_2 (or_2_out, button_2_out, Contador);
  Button button_3 (.out(button_3_out));
  or or_3 (or_3_out, button_3_out, RevertCount);
  Counter #(.width(12), .trigger("falling")) counter_1 (
    .load(or_3_out), .carry(counter_1_carry), .clk(or_2_out), .clr(or_1_out));  // open: D, count, Q
  Counter #(.width(4), .max('h2), .trigger("falling")) counter_2 (
    .load(or_3_out), .Q(counter_2_q), .clk(counter_3_carry), .clr(or_4_out));  // open: D, count, carry
  or or_4 (or_4_out, counter_1_carry, or_1_out);
  Counter #(.width(4), .max('h9), .trigger("falling")) counter_3 (
    .load(or_3_out), .Q(counter_3_q), .carry(counter_3_carry), .clk(counter_4_carry), .clr(or_4_out));  // open: D, count
  Counter #(.width(4), .max('h9), .trigger("falling")) counter_4 (
    .load(or_3_out), .Q(counter_4_q), .carry(counter_4_carry), .clk(or_2_out), .clr(or_4_out));  // open: D, count
  DigitsDisplay digitsdisplay_1 (
    .Bit3(counter_4_q[3]), .Bit2(counter_4_q[2]), .Bit1(counter_4_q[1]), .Bit0(counter_4_q[0]), .a(u1),
    .b(u2), .c(u3), .d(u4), .e(u5), .f(u6), .g(u7));
  DigitsDisplay digitsdisplay_2 (
    .Bit3(counter_3_q[3]), .Bit2(counter_3_q[2]), .Bit1(counter_3_q[1]), .Bit0(counter_3_q[0]), .a(d1),
    .b(d2), .c(d3), .d(d4), .e(d5), .f(d6), .g(d7));
  DigitsDisplay digitsdisplay_3 (
    .Bit3(counter_2_q[3]), .Bit2(counter_2_q[2]), .Bit1(counter_2_q[1]), .Bit0(counter_2_q[0]), .a(c1),
    .b(c2), .c(c3), .d(c4), .e(c5), .f(c6), .g(c7));

  // Notes on the sheet:
  //   Geral
  //   Centenas
  //   dezenas
  //   unidades
  //   Unidades
  //   dezenas
  //   centenas
endmodule

module DigitsDisplay (
  input  Bit3,
  input  Bit2,
  input  Bit1,
  input  Bit0,
  output a,
  output b,
  output c,
  output d,
  output e,
  output f,
  output g
);

  wire and_1_out, and_2_out, and_3_out, and_4_out, and_5_out, and_6_out, and_7_out, and_8_out, and_9_out,
       and_10_out, and_11_out, and_12_out, and_13_out, and_14_out, and_15_out, and_16_out, and_17_out,
       not_1_out, not_2_out, not_3_out, not_4_out, not_5_out, not_6_out, not_7_out, not_8_out, not_9_out,
       not_10_out, not_11_out, not_12_out, not_13_out, not_14_out, not_15_out, not_16_out, not_17_out,
       not_18_out, not_19_out, not_20_out, not_21_out, not_22_out, not_23_out, not_24_out, not_25_out,
       not_26_out, not_27_out, not_28_out, not_29_out, not_30_out, not_31_out, not_32_out, not_33_out,
       not_34_out, not_35_out, not_36_out, not_37_out, not_38_out, not_39_out, not_40_out, or_1_out,
       or_2_out, or_3_out, or_4_out, or_5_out, or_6_out, or_7_out, or_11_out, or_12_out, or_13_out;

  not not_1 (not_1_out, Bit2);
  and and_1 (and_1_out, not_1_out, not_2_out);
  not not_2 (not_2_out, Bit0);
  not not_3 (not_3_out, Bit3);
  and and_2 (and_2_out, not_3_out, Bit1);
  and and_3 (and_3_out, Bit2, Bit0);
  and and_4 (and_4_out, Bit3, not_4_out);
  not not_4 (not_4_out, Bit1);
  not not_5 (not_5_out, Bit2);
  not not_6 (not_6_out, Bit1);
  and and_5 (and_5_out, not_6_out, not_7_out);
  not not_7 (not_7_out, Bit0);
  not not_8 (not_8_out, Bit3);
  and and_6 (and_6_out, not_8_out, Bit1, Bit0);
  and and_7 (and_7_out, Bit3, not_9_out);
  not not_9 (not_9_out, Bit1);
  and and_8 (and_8_out, Bit3, not_10_out);
  not not_10 (not_10_out, Bit0);
  not not_11 (not_11_out, Bit3);
  and and_9 (and_9_out, not_11_out, not_12_out);
  not not_12 (not_12_out, Bit1);
  and and_10 (and_10_out, Bit2, Bit1);
  and and_11 (and_11_out, Bit3, not_13_out);
  not not_13 (not_13_out, Bit2);
  not not_14 (not_14_out, Bit2);
  and and_12 (and_12_out, not_14_out, not_15_out);
  not not_15 (not_15_out, Bit0);
  not not_16 (not_16_out, Bit3);
  not not_17 (not_17_out, Bit2);
  and and_13 (and_13_out, not_16_out, not_17_out, Bit1);
  not not_18 (not_18_out, Bit3);
  and and_14 (and_14_out, not_18_out, Bit1, not_19_out);
  not not_19 (not_19_out, Bit0);
  not not_20 (not_20_out, Bit1);
  and and_15 (and_15_out, Bit2, not_20_out, Bit0);
  and and_16 (and_16_out, Bit3, not_21_out, not_22_out);
  not not_21 (not_21_out, Bit1);
  not not_22 (not_22_out, Bit0);
  and and_17 (and_17_out, Bit3, Bit2, Bit0);
  not not_23 (not_23_out, Bit0);
  or or_1 (or_1_out, Bit3, not_24_out, Bit1);
  not not_24 (not_24_out, Bit2);
  not not_25 (not_25_out, Bit3);
  or or_2 (or_2_out, not_25_out, not_26_out, not_27_out);
  not not_26 (not_26_out, Bit2);
  not not_27 (not_27_out, Bit1);
  or or_3 (or_3_out, Bit3, Bit2, not_28_out);
  not not_28 (not_28_out, Bit0);
  or or_4 (or_4_out, Bit3, Bit2, not_29_out);
  not not_29 (not_29_out, Bit1);
  not not_30 (not_30_out, Bit1);
  or or_5 (or_5_out, Bit3, not_30_out, not_31_out);
  not not_31 (not_31_out, Bit0);
  not not_32 (not_32_out, Bit1);
  or or_6 (or_6_out, Bit2, not_32_out, not_33_out);
  not not_33 (not_33_out, Bit0);
  not not_34 (not_34_out, Bit3);
  not not_35 (not_35_out, Bit2);
  or or_7 (or_7_out, not_34_out, not_35_out, Bit1);
  not not_36 (not_36_out, Bit2);
  not not_37 (not_37_out, Bit1);
  not not_38 (not_38_out, Bit0);
  not not_39 (not_39_out, Bit3);
  not not_40 (not_40_out, Bit1);
  or or_8 (a, and_1_out, and_2_out, and_3_out, and_4_out);
  or or_9 (b, not_5_out, and_5_out, and_6_out, and_7_out, and_8_out);
  or or_10 (c, and_9_out, Bit0, and_10_out, and_11_out);
  and and_18 (e, not_23_out, or_1_out, or_2_out);
  and and_19 (f, or_3_out, or_4_out, or_5_out, or_6_out, or_7_out);
  or or_11 (or_11_out, Bit3, Bit2, Bit1);
  and and_20 (g, or_11_out, or_12_out, or_13_out);
  or or_12 (or_12_out, Bit3, not_36_out, not_37_out, not_38_out);
  or or_13 (or_13_out, not_39_out, Bit2, not_40_out);
  or or_14 (d, and_12_out, and_13_out, and_14_out, and_15_out, and_16_out, and_17_out);
endmodule

module Rule_2 (
  input  Bit1_Proposicao_PremMaior,
  input  Bit0_Proposicao_PremMaior,
  input  Bit1_Proposicao_PremMenor,
  input  Bit0_Proposicao_PremMenor,
  input  Bit1_Figura,
  input  Bit0_Figura,
  output ViolaRegra2
);

  wire bool_is_mediumtermdistbted_1_simltermomediodistrbuido;

  bool_Is_MediumTermDistbted bool_is_mediumtermdistbted_1 (
    .Bit1_Proposicao_PremMaior(Bit1_Proposicao_PremMaior),
    .Bit0_Proposicao_PremMaior(Bit0_Proposicao_PremMaior),
    .Bit1_Proposicao_PremMenor(Bit1_Proposicao_PremMenor),
    .Bit0_Proposicao_PremMenor(Bit0_Proposicao_PremMenor), .Bit1_Figura(Bit1_Figura),
    .Bit0_Figura(Bit0_Figura),
    .SimlTermoMedioDistrbuido(bool_is_mediumtermdistbted_1_simltermomediodistrbuido));
  not not_1 (ViolaRegra2, bool_is_mediumtermdistbted_1_simltermomediodistrbuido);
endmodule

module Rule_3 (
  input  Bit1_PremMaior,
  input  Bit0_PremMaior,
  input  Bit1_Figura,
  input  Bit0_Figura,
  input  Bit1_PremMenor,
  input  Bit0_PremMenor,
  input  Bit1_Conclusao,
  input  Bit0_Conclusao,
  output FalaciaProcIlicitoTermoMaior,
  output FalaciaProcIlicitoTermoMenor
);

  wire boolDistribuiPredicado_simdistribuipredicado, boolDistribuiSujeito_simdistribuisujeito,
       boolDistrPredicNaPremMaior_simpredicdodistrbuidonapmaior,
       boolSujeitoDistribNaPremMenor_simsujeitodistrbuidonapmenor, not_1_out, not_2_out;

  bool_Is_DistrbPredicOnMajorPremiss boolDistrPredicNaPremMaior (
    .Bit1_Proposicao_PremMaior(Bit1_PremMaior), .Bit0_Proposicao_PremMaior(Bit0_PremMaior),
    .Bit1_Figura(Bit1_Figura), .Bit0_Figura(Bit0_Figura),
    .SimPredicdoDistrbuidoNaPMaior(boolDistrPredicNaPremMaior_simpredicdodistrbuidonapmaior));
  bool_Is_SubjtDistribOnMinorPremiss boolSujeitoDistribNaPremMenor (
    .Bit1_Proposicao_PremMenor(Bit1_PremMenor), .Bit0_Proposicao_PremMenor(Bit0_PremMenor),
    .Bit1_Figura(Bit1_Figura), .Bit0_Figura(Bit0_Figura),
    .SimSujeitoDistrbuidoNaPMenor(boolSujeitoDistribNaPremMenor_simsujeitodistrbuidonapmenor));
  bool_Is_DistributdPredicate boolDistribuiPredicado (
    .Bit1(Bit1_Conclusao), .Bit0(Bit0_Conclusao),
    .SimDistribuiPredicado(boolDistribuiPredicado_simdistribuipredicado));
  bool_Is_DistributdSubject boolDistribuiSujeito (
    .bit1(Bit1_Conclusao), .bit0(Bit0_Conclusao),
    .simDistribuiSujeito(boolDistribuiSujeito_simdistribuisujeito));
  not not_1 (not_1_out, boolDistrPredicNaPremMaior_simpredicdodistrbuidonapmaior);
  not not_2 (not_2_out, boolSujeitoDistribNaPremMenor_simsujeitodistrbuidonapmenor);
  and and_1 (FalaciaProcIlicitoTermoMaior, not_1_out, boolDistribuiPredicado_simdistribuipredicado);
  and and_2 (FalaciaProcIlicitoTermoMenor, not_2_out, boolDistribuiSujeito_simdistribuisujeito);
endmodule

module Rule_4 (
  input  Bit1_PremMaior,
  input  Bit0_PremMaior,
  input  Bit1_PremMenor,
  input  Bit0_PremMenor,
  output FalaciaDasPremissasExclusivas
);

  wire boolPremMaiorNegativa_simpremmaiornegativa, boolPremMenorNegativa_simpremmenornegativa;

  bool_Is_MajorPremNegative boolPremMaiorNegativa (
    .Bit1_PremMaior(Bit1_PremMaior), .Bit0_PremMaior(Bit0_PremMaior),
    .SimPremMaiorNegativa(boolPremMaiorNegativa_simpremmaiornegativa));
  bool_Is_MinorPremNegative boolPremMenorNegativa (
    .Bit1_PremMenor(Bit1_PremMenor), .Bit0_PremMenor(Bit0_PremMenor),
    .SimPremMenorNegativa(boolPremMenorNegativa_simpremmenornegativa));
  and and_1 (FalaciaDasPremissasExclusivas, boolPremMaiorNegativa_simpremmaiornegativa, boolPremMenorNegativa_simpremmenornegativa);
endmodule

module Rule_5 (
  input  Bit1_PremMaior,
  input  Bit0_PremMaior,
  input  Bit1_PremMenor,
  input  Bit0_PremMenor,
  input  Bit1_Conclusao,
  input  Bit0_Conclusao,
  output FalaciaDaConclusaoAfirmtvaAPartirPremNegativ
);

  wire boolConclusaoNaoNegativa_simconclusaoafirmativa, boolPremMaiorNegativa_simpremmaiornegativa,
       boolPremMenorNegativa_simpremmenornegativa, or_1_out;

  bool_Is_MajorPremNegative boolPremMaiorNegativa (
    .Bit1_PremMaior(Bit1_PremMaior), .Bit0_PremMaior(Bit0_PremMaior),
    .SimPremMaiorNegativa(boolPremMaiorNegativa_simpremmaiornegativa));
  bool_Is_MinorPremNegative boolPremMenorNegativa (
    .Bit1_PremMenor(Bit1_PremMenor), .Bit0_PremMenor(Bit0_PremMenor),
    .SimPremMenorNegativa(boolPremMenorNegativa_simpremmenornegativa));
  boolAfirmatvConclusion boolConclusaoNaoNegativa (
    .Bit1_Conclusao(Bit1_Conclusao), .Bit0_Conclusao(Bit0_Conclusao),
    .SimConclusaoAfirmativa(boolConclusaoNaoNegativa_simconclusaoafirmativa));
  or or_1 (or_1_out, boolPremMaiorNegativa_simpremmaiornegativa, boolPremMenorNegativa_simpremmenornegativa);
  and and_1 (FalaciaDaConclusaoAfirmtvaAPartirPremNegativ, or_1_out, boolConclusaoNaoNegativa_simconclusaoafirmativa);
endmodule

module Rule_6 (
  input  Bit1_PremMaior,
  input  Bit0_PremMaior,
  input  Bit1_PremMenor,
  input  Bit0_PremMenor,
  input  Bit1_Conclusao,
  input  Bit0_Conclusao,
  output FalaciaExistencial
);

  wire boolConclusaoParticular_simconclusaoparticular, boolPremMaiorUnivrsl_simpremmaioruniversal,
       boolPremMenorUniversal_simpremmenoruniversal;

  bool_Universal_Major_Premiss boolPremMaiorUnivrsl (
    .Bit1_PremMaior(Bit1_PremMaior), .Bit0_PremMaior(Bit0_PremMaior),
    .SimPremMaiorUniversal(boolPremMaiorUnivrsl_simpremmaioruniversal));
  bool_Universal_Minor_Premiss boolPremMenorUniversal (
    .Bit1_PremMenor(Bit1_PremMenor), .Bit0_PremMenor(Bit0_PremMenor),
    .SimPremMenorUniversal(boolPremMenorUniversal_simpremmenoruniversal));
  bool_IsEspecificConclusion boolConclusaoParticular (
    .Bit1_Conclusao(Bit1_Conclusao), .Bit0_Conclusao(Bit0_Conclusao),
    .SimConclusaoParticular(boolConclusaoParticular_simconclusaoparticular));
  and and_1 (FalaciaExistencial, boolPremMaiorUnivrsl_simpremmaioruniversal, boolPremMenorUniversal_simpremmenoruniversal, boolConclusaoParticular_simconclusaoparticular);
endmodule

module bool_Is_Argument_Valid (
  input  regra2,
  input  regra3,
  input  regra3b,
  input  Reset,
  input  regra4,
  input  regra5,
  input  regra6,
  output SimArgumentoValido,
  output [5:0] out_9,
  output Valids_Counter
);

  wire and_2_out, and_3_out, clock_1_out, d_ff_1_q, d_ff_2_q, d_ff_2_qn, not_1_out, not_2_out, not_3_out,
       not_4_out, not_5_out, not_6_out;

  not not_1 (not_1_out, regra2);
  not not_2 (not_2_out, regra3);
  not not_3 (not_3_out, regra3b);
  not not_4 (not_4_out, regra4);
  not not_5 (not_5_out, regra5);
  not not_6 (not_6_out, regra6);
  and and_1 (SimArgumentoValido, not_1_out, not_2_out, not_3_out, not_4_out, not_5_out, not_6_out);
  and and_2 (and_2_out, SimArgumentoValido, d_ff_1_q);
  and and_3 (and_3_out, SimArgumentoValido, d_ff_2_q);
  Clock clock_1 (.out(clock_1_out));
  D_Flip_Flop d_ff_1 (.clk(clock_1_out), .Q(d_ff_1_q), .preset(and_3_out), .reset(d_ff_2_q));  // open: D, Qn, en
  D_Flip_Flop d_ff_2 (
    .clk(clock_1_out), .Q(d_ff_2_q), .Qn(d_ff_2_qn), .preset(and_2_out), .reset(d_ff_1_q));  // open: D, en
  or or_1 (Valids_Counter, d_ff_1_q, d_ff_2_qn);
  Counter #(.width(6), .max('h23)) counter_1 (
    .Q(out_9), .clk(Valids_Counter), .clr(Reset));  // open: load, D, count, carry
endmodule
